// Logisim project PFC.circ as structural Verilog: 4 circuits, main circuit main
module main (
  input  Load,
  input  Start,
  input  Reset,
  input  in_4,
  input  in_5
);

  wire clock_2_out, clock_3_out, clock_4_out, clock_5_out, clock_6_out, clock_7_out, Op_alu, Op_alui,
       Program_load, Stop_load, WR_EW_0, WR_EW_1;
  wire [3:0] ALU_op, Cond;
  wire [7:0] ALU_res, Bus_A, Bus_B, Bus_D, EW_0, imm8, multiplexer_5_out, ROM_out, Rs2_out, Rs3_out, WB_0;
  wire [15:0] IR, Jump_dest, MAR, multiplexer_2_out, multiplexer_3_out, PC, PC_next, PC_plus_4, ROM_address;
  wire [15:12] imm16;
  wire [31:0] Mem_inst_out;

  Clock clock_1 ();  // open: out
  S_R_Flip_Flop s_r_ff_1 (.S(Load), .R(Stop_load), .clk(clock_2_out), .Q(Program_load));  // open: reset, Qn, preset
  Clock clock_2 (.out(clock_2_out));
  ROM #(.addrWidth(16)) rom_1 (.addr(ROM_address), .data(ROM_out));
  Register #(.width(16)) u_PC (.D(PC_next), .en(in_4), .clk(clock_3_out), .Q(PC));  // open: clr
  Clock clock_3 (.out(clock_3_out));
  Clock clock_4 (.out(clock_4_out));
  Multiplexer #(.width(16)) multiplexer_1 (.in0(PC_plus_4), .in1(Jump_dest), .out(PC_next), .sel(in_5));
  Counter #(.max('hffff), .width(16)) counter_1 (
    .count(Program_load), .Q(ROM_address), .up(1'b1), .clk(clock_4_out));  // open: load, D, carry, clr
  Adder #(.width(16)) adder_1 (.a(PC), .b(16'h4), .out(PC_plus_4), .cin(1'b0));  // open: cout
  Comparator #(.mode("unsigned"), .width(16)) comparator_1 (
    .a(ROM_address), .b(16'h80), .eq(Stop_load));  // open: gt, lt
  Register #(.width(32)) u_IR (
    .D(Mem_inst_out), .en(in_4), .clk(clock_5_out), .Q({imm16, ALU_op, imm8, IR[15:8], Cond, IR[3:0]}));  // open: clr
  Clock clock_5 (.out(clock_5_out));
  Register_File register_file_1 (
    .Rd(IR[11:8]), .Rs1(IR[15:12]), .Rs2(imm8[3:0]), .Rs3(imm8[7:4]), .WB_0(WB_0), .Rs1_out(Bus_A),
    .Rs2_out(Rs2_out), .Rs3_out(Rs3_out));  // open: WB_1
  Register u_EW_0 (.D(ALU_res), .en(WR_EW_0), .clk(clock_6_out), .Q(EW_0));  // open: clr
  Clock clock_6 (.out(clock_6_out));
  Multiplexer #(.width(16)) multiplexer_2 (.in0(PC), .in1(MAR), .out(multiplexer_2_out), .sel(1'b0));
  Multiplexer #(.width(16)) multiplexer_3 (
    .in0(multiplexer_2_out), .in1(ROM_address), .out(multiplexer_3_out), .sel(Program_load));
  Multiplexer #(.width(8)) multiplexer_4 (.in0(Rs2_out), .in1(imm8), .out(Bus_B));  // open: sel
  Multiplexer #(.width(8)) multiplexer_5 (.in0(Bus_D), .in1(ROM_out), .out(multiplexer_5_out), .sel(Program_load));
  Decoder #(.select(4)) decoder_1 (
    .out0(Op_alu), .out1(Op_alui), .sel(IR[3:0]));  // open: out2, out3, out4, out5, out6, out7, out8, out9, out10, out11, out12, out13, out14, out15, en
  Register EW_1 (.en(WR_EW_1), .clk(clock_7_out));  // open: D, Q, clr
  Clock clock_7 (.out(clock_7_out));
  Memory memory_1 (
    .Address(multiplexer_3_out), .Fetch(in_4), .Write(Program_load), .Din(multiplexer_5_out),
    .Inst0(Mem_inst_out[7:0]), .Inst1(Mem_inst_out[15:8]), .Inst2(Mem_inst_out[23:16]),
    .Inst3(Mem_inst_out[31:24]));  // open: Read, Dout
  ALU alu_1 (.LHS(Bus_A), .RHS(Bus_B), .Op(ALU_op), .Result(ALU_res));

  // Other names for the same wires on the sheet: Fetch = in_4; imm16[11:0] = {ALU_op, imm8};
  //   IR (some bits) = {imm16, ALU_op, imm8, Cond}; Rs2[3:0] = imm8[3:0]; Rs3[3:0] = imm8[7:4];
  //   IR_27_24[3:0] = ALU_op; IR_31_28[3:0] = imm16; Opcode[3:0] = IR[3:0]; Rd[3:0] = IR[11:8]; Rs1[3:0] = IR[15:12];
  //   Jump = in_5; Rs1_out[7:0] = Bus_A

  // Notes on the sheet:
  //   contents of rom_1 (hex, n*v repeats v):
  //   1 1 f 0 1 2 33 0 1 3 55 0 0 41 0 0 0 52 0 0 0 63 5*0 f
endmodule

module Memory (
  input  [15:0] Address,
  input  Fetch,
  input  Read,
  input  Write,
  input  [7:0] Din,
  output [7:0] Dout,
  output [7:0] Inst0,
  output [7:0] Inst1,
  output [7:0] Inst2,
  output [7:0] Inst3
);

  wire En_0, En_1, En_2, En_3;

  Decoder #(.select(2)) decoder_1 (.out0(En_0), .out1(En_1), .out2(En_2), .out3(En_3), .sel(Address[1:0]));  // open: en
  // RAM #(.addrWidth(14), .databus("bidir"), .enables("line"), .trigger("high")) ram_1: pin names not known; wires that end beside it: Address[15:2], Fetch, Write, En_0, Inst0
  // RAM #(.addrWidth(14), .databus("bidir"), .enables("line"), .trigger("high")) ram_2: pin names not known; wires that end beside it: Address[15:2], Fetch, Write, En_1, Inst0
  // RAM #(.addrWidth(14), .databus("bidir"), .enables("line"), .trigger("high")) ram_3: pin names not known; wires that end beside it: Address[15:2], Fetch, Write, En_2, Inst0
  // RAM #(.addrWidth(14), .databus("bidir"), .enables("line"), .trigger("high")) ram_4: pin names not known; wires that end beside it: Address[15:2], Fetch, Write, En_3, Inst0
  assign Inst0 = Write ? Din : 8'bz;  // Controlled_Buffer controlled_buffer_1

  assign Inst1 = Inst0;
  assign Inst2 = Inst0;
  assign Inst3 = Inst0;

  // Other names for the same wires on the sheet: RAM_0[7:0] = Inst0; RAM_1[7:0] = Inst0; RAM_2[7:0] = Inst0;
  //   RAM_3[7:0] = Inst0
endmodule

module Register_File (
  input  [3:0] Rd,
  input  [3:0] Rs1,
  input  [3:0] Rs2,
  input  [3:0] Rs3,
  input  [7:0] WB_0,
  input  [7:0] WB_1,
  output [7:0] Rs1_out,
  output [7:0] Rs2_out,
  output [7:0] Rs3_out
);

  wire clock_1_out;

  Register r1 (.clk(clock_1_out));  // open: D, en, Q, clr
  Clock clock_1 (.out(clock_1_out));
endmodule

module ALU (
  input  [7:0] LHS,
  input  [7:0] RHS,
  input  [3:0] Op,
  output [7:0] Result
);

  Adder adder_1 (.a(LHS), .b(RHS), .out(Result), .cin(1'b0));  // open: cout
endmodule
