// Logisim project PFC.circ as structural Verilog: 2 circuits, main circuit main
module main (
  input  Start,
  input  Load_program,
  input  Reset
);

  wire adder_1_cout, Bus_ALU, clock_2_out, clock_3_out, clock_4_out, clock_5_out, clock_6_out, clock_7_out,
       clock_8_out, clock_9_out, clock_10_out, clock_11_out, clock_12_out, clock_13_out, decoder_1_out0,
       decoder_1_out2, decoder_1_out5, execute, fetch, fetch_1, fetch_2, fetch_3, or_1_out, or_2_out,
       or_3_out, or_4_out;
  wire [2:0] ADDR, cpu_state;
  wire [4:0] SF;
  wire [6:0] WR;
  wire [7:0] A, B, Data_bus, H, imm8, imm16, L, Memory, multiplexer_1_out, Opcode, PCH, PCH_next, PCL,
       PCL_next, Program_data, RD, SP, SP_next;
  wire [15:0] Address_bus, controlled_buffer_10_out, Loader_counter, multiplexer_2_out, undriven;
  wire [23:0] Control_signals;

  Clock clock_1 ();  // open: out
  LED led_1 (.in(fetch_1));
  LED led_2 (.in(fetch_2));
  LED led_3 (.in(fetch_3));
  LED led_4 (.in(execute));
  Clock clock_2 (.out(clock_2_out));
  Counter #(.max('hffff), .width(16)) counter_1 (
    .count(Load_program), .Q(Loader_counter), .up(1'b1), .clk(clock_2_out), .clr(Reset));  // open: load, D, carry
  or or_1 (or_1_out, Load_program, 1'b0);
  or or_2 (or_2_out, fetch, 1'b0);
  Multiplexer #(.width(8)) multiplexer_1 (.in0(Opcode), .in1(Memory), .out(multiplexer_1_out), .sel(fetch_1));
  Pull_Resistor pull_resistor_1 (.node({SF, ADDR, Bus_ALU, RD, WR}));
  assign {SF, ADDR, Bus_ALU, RD, WR} = execute ? Control_signals : 24'bz;  // Controlled_Buffer controlled_buffer_1
  ROM #(.addrWidth(16)) Program (.addr(Loader_counter), .data(Program_data));
  Multiplexer #(.width(16)) multiplexer_2 (
    .in0(Address_bus), .in1(Loader_counter), .out(multiplexer_2_out), .sel(Load_program));
  RAM #(.addrWidth(16), .databus("bidir"), .enables("line")) u_Memory (
    .addr(multiplexer_2_out), .we(or_1_out), .oe(or_2_out), .clk(clock_3_out), .data(Memory));
  Clock clock_3 (.out(clock_3_out));
  assign Memory = Load_program ? Program_data : 8'bz;  // Controlled_Buffer controlled_buffer_2
  Control_Unit control_unit_1 (
    .start(Start), .Opcode(multiplexer_1_out), .reset(Reset), .CPU_state(cpu_state),
    .Control_signals(Control_signals));
  Register reg0_A (.D(Data_bus), .en(WR[0]), .clk(clock_4_out), .Q(A), .clr(Reset));
  Clock clock_4 (.out(clock_4_out));
  Register reg2_L (.D(Data_bus), .en(WR[2]), .clk(clock_5_out), .Q(L), .clr(Reset));
  Clock clock_5 (.out(clock_5_out));
  Register reg8_PCL (.D(PCL_next), .en(or_3_out), .clk(clock_6_out), .Q(PCL), .clr(Reset));
  or or_3 (or_3_out, fetch, WR[5]);
  Clock clock_6 (.out(clock_6_out));
  Adder adder_1 (.a(PCL), .b(8'h1), .out(PCL_next), .cin(1'b0), .cout(adder_1_cout));
  Adder adder_2 (.a(PCH), .b({8{1'b0}}), .out(PCH_next), .cin(adder_1_cout));  // open: cout
  Decoder #(.enable("false"), .select(3)) decoder_1 (
    .out0(decoder_1_out0), .out2(decoder_1_out2), .out3(execute), .out4(fetch_1), .out5(decoder_1_out5),
    .out6(fetch_2), .out7(fetch_3), .sel(cpu_state));  // open: out1
  Register reg1_B (.D(Data_bus), .en(WR[1]), .clk(clock_7_out), .Q(B), .clr(Reset));
  Clock clock_7 (.out(clock_7_out));
  Register reg3_H (.D(Data_bus), .en(WR[3]), .clk(clock_8_out), .Q(H), .clr(Reset));
  Clock clock_8 (.out(clock_8_out));
  Register reg_SP (.D(SP_next), .clk(clock_9_out), .Q(SP));  // open: en, clr
  Clock clock_9 (.out(clock_9_out));
  Register reg9_PCH (.D(PCH_next), .en(or_4_out), .clk(clock_10_out), .Q(PCH), .clr(Reset));
  or or_4 (or_4_out, fetch, WR[6]);
  Clock clock_10 (.out(clock_10_out));
  Register u_Opcode (.D(Memory), .en(fetch_1), .clk(clock_11_out), .Q(Opcode), .clr(Reset));
  Clock clock_11 (.out(clock_11_out));
  Register Operand_1 (.D(Memory), .en(fetch_2), .clk(clock_12_out), .Q(imm8), .clr(Reset));
  Clock clock_12 (.out(clock_12_out));
  Register Operand_2 (.D(Memory), .en(fetch_3), .clk(clock_13_out), .Q(imm16), .clr(Reset));
  Clock clock_13 (.out(clock_13_out));
  or or_5 (fetch, fetch_1, fetch_2, fetch_3);
  assign Data_bus = RD[0] ? A : 8'bz;  // Controlled_Buffer controlled_buffer_3
  assign Data_bus = RD[1] ? B : 8'bz;  // Controlled_Buffer controlled_buffer_4
  assign Data_bus = RD[2] ? L : 8'bz;  // Controlled_Buffer controlled_buffer_5
  assign Data_bus = RD[3] ? H : 8'bz;  // Controlled_Buffer controlled_buffer_6
  assign Data_bus = RD[7] ? imm8 : 8'bz;  // Controlled_Buffer controlled_buffer_7
  assign Data_bus = RD[5] ? PCL : 8'bz;  // Controlled_Buffer controlled_buffer_8
  assign Data_bus = RD[6] ? PCH : 8'bz;  // Controlled_Buffer controlled_buffer_9
  assign controlled_buffer_10_out = Bus_ALU ? undriven : 16'bz;  // Controlled_Buffer controlled_buffer_10
  assign Address_bus = fetch ? {PCH, PCL} : 16'bz;  // Controlled_Buffer controlled_buffer_11
  assign Address_bus = ADDR[0] ? {H, L} : 16'bz;  // Controlled_Buffer controlled_buffer_12
  assign Address_bus = ADDR[1] ? {imm8, imm16} : 16'bz;  // Controlled_Buffer controlled_buffer_13
  assign Address_bus = ADDR[2] ? {{8{1'b1}}, SP} : 16'bz;  // Controlled_Buffer controlled_buffer_14
  Pull_Resistor pull_resistor_2 (.node(Address_bus));

  // Other names for the same wires on the sheet: WR_A = WR[0]; WR_B = WR[1]; WR_L = WR[2]; WR_H = WR[3];
  //   WR_MEM = WR[4]; WR_PCL = WR[5]; WR_PCH = WR[6]; RD_A = RD[0]; RD_B = RD[1]; RD_L = RD[2]; RD_H = RD[3];
  //   RD_MEM = RD[4]; RD_PCL = RD[5]; RD_PCH = RD[6]; RD_imm8 = RD[7]; ADDR_HL = ADDR[0]; ADDR_imm16 = ADDR[1];
  //   ADDR_SP = ADDR[2]; Operand_2[7:0] = imm16; imm16[15:8] = imm8; Operand_1[7:0] = imm8

  // Notes on the sheet:
  //   contents of Program (hex, n*v repeats v):
  //   10 2 11 3 81
endmodule

module Control_Unit (
  input  start,
  input  [7:0] Opcode,
  input  reset,
  output [2:0] CPU_state,
  output [23:0] Control_signals
);

  wire ALU_b, ALU_u, and_1_out, and_2_out, and_5_out, and_7_out, CALL_dest, clock_1_out, CLx, CMP,
       decoder_2_out2, decoder_2_out3, decoder_5_out0, decoder_7_out0, decoder_7_out1, decoder_7_out2,
       decoder_7_out3, decoder_7_out4, IMM_Rd_imm, INT, IRET, JMP, Jxx, LD_Rd, LD_Rd_addr, len_3, MOV_Rd_Rs,
       not_3_out, not_4_out, not_6_out, op_00, op_001, op_01, optional_imm8, or_4_out, or_5_out, or_17_out,
       POP_Rd, PUSH_Rs, RD_op_1_0, RET, ST_Rs, ST_Rs_addr, STx, TEST, WR_op_1_0;
  wire [1:0] inst_length, multiplexer_2_out;
  wire [1:1] not_1_out;
  wire [2:0] cpu_next_state, multiplexer_1_out;
  wire [2:2] not_2_out;

  Decoder #(.enable("false"), .select(2)) decoder_1 (
    .out0(op_00), .out1(op_01), .out2(ALU_b), .out3(ALU_u), .sel(Opcode[7:6]));
  or or_1 (op_001, decoder_2_out2, decoder_2_out3);
  Decoder #(.select(2)) decoder_2 (
    .out0(MOV_Rd_Rs), .out1(IMM_Rd_imm), .out2(decoder_2_out2), .out3(decoder_2_out3), .sel(Opcode[5:4]),
    .en(op_00));
  Decoder #(.select(3)) decoder_3 (
    .out0(ST_Rs), .out1(ST_Rs_addr), .out2(LD_Rd), .out3(LD_Rd_addr), .out4(PUSH_Rs), .out5(POP_Rd),
    .out6(CALL_dest), .out7(RET), .sel(Opcode[4:2]), .en(op_001));
  Decoder #(.select(3)) decoder_4 (
    .out0(CMP), .out1(TEST), .out2(CLx), .out3(STx), .out4(JMP), .out5(Jxx), .out6(INT), .out7(IRET),
    .sel(Opcode[5:3]), .en(op_01));
  not not_1 (not_1_out[1], INT);
  not not_2 (not_2_out[2], 1'b0);
  and and_1 (and_1_out, optional_imm8, Opcode[2]);
  Register #(.width(3)) z_CPU_state (.D(cpu_next_state), .en(1'b1), .clk(clock_1_out), .Q(CPU_state), .clr(reset));
  Clock clock_1 (.out(clock_1_out));
  or or_2 (Control_signals[14], and_1_out, IMM_Rd_imm);
  or or_3 (len_3, ST_Rs_addr, LD_Rd_addr, CALL_dest, JMP, Jxx);
  Multiplexer #(.select(3), .width(3)) multiplexer_1 (
    .in0({start, 2'b00}), .in2({INT, not_1_out[1], 1'b0}), .in3({not_2_out[2], 2'b00}),
    .in4({1'b1, inst_length}), .in5(3'b011), .in6(3'b101), .in7(3'b110), .out(multiplexer_1_out),
    .sel(CPU_state));  // open: in1
  not not_3 (not_3_out, 1'b0);
  or or_4 (or_4_out, WR_op_1_0, MOV_Rd_Rs);
  and and_2 (and_2_out, multiplexer_1_out[2], not_3_out);
  and and_3 (cpu_next_state[2], and_2_out, not_4_out);
  or or_5 (or_5_out, multiplexer_1_out[1], 1'b0);
  and and_4 (cpu_next_state[1], or_5_out, not_4_out);
  and and_5 (and_5_out, multiplexer_1_out[0], not_3_out);
  and and_6 (cpu_next_state[0], and_5_out, not_4_out);
  not not_4 (not_4_out, 1'b0);
  or or_6 (inst_length[1], Control_signals[14], len_3);
  not not_5 (inst_length[0], Control_signals[14]);
  Decoder #(.select(2)) decoder_5 (
    .out0(decoder_5_out0), .out1(Control_signals[1]), .out2(Control_signals[2]), .out3(Control_signals[3]),
    .sel(multiplexer_2_out), .en(or_4_out));
  Multiplexer #(.width(2)) multiplexer_2 (
    .in0(Opcode[1:0]), .in1(Opcode[3:2]), .out(multiplexer_2_out), .sel(MOV_Rd_Rs));
  or or_7 (WR_op_1_0, LD_Rd, LD_Rd_addr, IMM_Rd_imm, POP_Rd, ALU_u);
  or or_8 (Control_signals[4], ST_Rs, ST_Rs_addr, PUSH_Rs);
  or or_9 (Control_signals[0], ALU_b, decoder_5_out0);
  and and_7 (and_7_out, optional_imm8, not_6_out);
  not not_6 (not_6_out, Opcode[2]);
  Decoder #(.select(2)) decoder_6 (
    .out0(Control_signals[7]), .out1(Control_signals[8]), .out2(Control_signals[9]),
    .out3(Control_signals[10]), .sel(Opcode[1:0]), .en(RD_op_1_0));
  or or_10 (optional_imm8, CMP, TEST, ALU_b);
  or or_11 (RD_op_1_0, MOV_Rd_Rs, ST_Rs, ST_Rs_addr, ALU_u, and_7_out);
  or or_12 (Control_signals[11], LD_Rd, LD_Rd_addr, POP_Rd);
  or or_13 (Control_signals[16], ST_Rs, LD_Rd);
  or or_14 (Control_signals[17], ST_Rs_addr, LD_Rd_addr);
  or or_15 (Control_signals[18], PUSH_Rs, POP_Rd);
  or or_16 (Control_signals[15], ALU_u, ALU_b);
  Decoder #(.select(3)) decoder_7 (
    .out0(decoder_7_out0), .out1(decoder_7_out1), .out2(decoder_7_out2), .out3(decoder_7_out3),
    .out4(decoder_7_out4), .sel(Opcode[5:3]), .en(or_17_out));  // open: out5, out6, out7
  or or_17 (or_17_out, CLx, STx);
  or or_18 (Control_signals[19], decoder_7_out0, TEST, CMP);
  or or_19 (Control_signals[20], decoder_7_out1, TEST, CMP);
  or or_20 (Control_signals[21], decoder_7_out2, CMP);
  or or_21 (Control_signals[22], decoder_7_out3, CMP);
  or or_22 (Control_signals[23], decoder_7_out4, INT, CMP);

  assign {Control_signals[13:12], Control_signals[6:5]} = 4'b0000;

  // Other names for the same wires on the sheet: WR[4:0] = Control_signals[4:0]; WR_MEM = Control_signals[4];
  //   RD (some bits) = {Control_signals[14], Control_signals[11:7]}; RD_MEM = Control_signals[11];
  //   len_2 = Control_signals[14]; RD_imm8_t = Control_signals[14]; Bus_ALU = Control_signals[15];
  //   ADDR[2:0] = Control_signals[18:16]; ADDR_HL = Control_signals[16]; ADDR_imm16 = Control_signals[17];
  //   ADDR_SP = Control_signals[18]; SF[4:0] = Control_signals[23:19]; WR_A = ALU_b; WR_op_3_2 = MOV_Rd_Rs
endmodule
