// Logisim project PFC_v2.circ as structural Verilog: 1 circuit, main circuit main
module main (
  input  in_1,
  input  in_2,
  input  in_3,
  input  in_4
);

  wire and_1_out, clock_1_out, clock_3_out, clock_4_out, clock_5_out, clock_6_out, clock_7_out, clock_8_out,
       clock_9_out, clock_10_out, clock_11_out, clock_12_out, clock_13_out, not_1_out, PC_inc, undriven;
  wire [7:0] A_q, B_q, D_Opcode, D_Operand_1, D_Operand_2, Data_bus, E_Operand_1, E_Operand_2, H_q, L_q,
       Memory_out, Program_Memory_data;
  wire [15:0] Address, MAR, PC, PC_next;
  wire [31:0] D_Controls, E_Controls;

  Register #(.width(16)) u_PC (.D(PC_next), .en(PC_inc), .clk(clock_1_out), .Q(PC));  // open: clr
  Clock clock_1 (.out(clock_1_out));
  Adder #(.width(16)) adder_1 (.a(PC), .b({16{1'b0}}), .out(PC_next), .cin(1'b1));  // open: cout
  or or_1 (PC_inc, in_1, in_2, in_3);
  Clock clock_2 ();  // open: out
  Multiplexer #(.width(16)) multiplexer_1 (.in0(PC), .in1(MAR), .out(Address), .sel(1'b0));
  Register #(.width(16)) u_MAR (.clk(clock_3_out), .Q(MAR));  // open: D, en, clr
  Clock clock_3 (.out(clock_3_out));
  ROM #(.dataWidth(32)) uCode (.addr(D_Opcode), .data(D_Controls));
  Register FD_Opcode (.D(Memory_out), .en(in_1), .clk(clock_4_out), .Q(D_Opcode));  // open: clr
  Clock clock_4 (.out(clock_4_out));
  Register #(.width(32)) DE_Controls (.D(D_Controls), .en(in_4), .clk(clock_5_out), .Q(E_Controls));  // open: clr
  Clock clock_5 (.out(clock_5_out));
  Register A (.D(Data_bus), .en(E_Controls[0]), .clk(clock_6_out), .Q(A_q));  // open: clr
  Clock clock_6 (.out(clock_6_out));
  Register B (.D(Data_bus), .en(E_Controls[1]), .clk(clock_7_out), .Q(B_q));  // open: clr
  Clock clock_7 (.out(clock_7_out));
  Register L (.D(Data_bus), .en(E_Controls[2]), .clk(clock_8_out), .Q(L_q));  // open: clr
  Clock clock_8 (.out(clock_8_out));
  Register H (.D(Data_bus), .en(E_Controls[3]), .clk(clock_9_out), .Q(H_q));  // open: clr
  Clock clock_9 (.out(clock_9_out));
  and and_1 (and_1_out, undriven, Address[15]);
  assign Data_bus = E_Controls[4] ? A_q : 8'bz;  // Controlled_Buffer controlled_buffer_1
  assign Data_bus = E_Controls[5] ? B_q : 8'bz;  // Controlled_Buffer controlled_buffer_2
  assign Data_bus = E_Controls[6] ? L_q : 8'bz;  // Controlled_Buffer controlled_buffer_3
  assign Data_bus = E_Controls[7] ? H_q : 8'bz;  // Controlled_Buffer controlled_buffer_4
  ROM #(.addrWidth(15)) Program_Memory (.addr(Address[14:0]), .data(Program_Memory_data));
  RAM #(.addrWidth(15), .databus("bidir"), .enables("line"), .misaligned("true"), .trigger("high")) Data_Memory (
    .addr(Address[14:0]), .data(Memory_out));  // open: we, oe, clk
  Register FD_Operand_1 (.D(Memory_out), .en(in_2), .clk(clock_10_out), .Q(D_Operand_1));  // open: clr
  Clock clock_10 (.out(clock_10_out));
  Register DE_Operand_1 (.D(D_Operand_1), .en(in_4), .clk(clock_11_out), .Q(E_Operand_1));  // open: clr
  Clock clock_11 (.out(clock_11_out));
  assign Data_bus = E_Controls[8] ? E_Operand_1 : 8'bz;  // Controlled_Buffer controlled_buffer_5
  Counter #(.max('hffff), .width(16)) SP ();  // open: clr, load, up, count, clk, D, carry, Q
  not not_1 (not_1_out, Address[15]);
  assign Memory_out = not_1_out ? Program_Memory_data : 8'bz;  // Controlled_Buffer controlled_buffer_6
  Register FD_Operand_2 (.D(Memory_out), .en(in_3), .clk(clock_12_out), .Q(D_Operand_2));  // open: clr
  Clock clock_12 (.out(clock_12_out));
  Register DE_Operand_2 (.D(D_Operand_2), .en(in_4), .clk(clock_13_out), .Q(E_Operand_2));  // open: clr
  Clock clock_13 (.out(clock_13_out));

  // Other names for the same wires on the sheet: Decode = in_4; WR_A = E_Controls[0]; WR_B = E_Controls[1];
  //   WR_L = E_Controls[2]; WR_H = E_Controls[3]; RD_A = E_Controls[4]; RD_B = E_Controls[5]; RD_L = E_Controls[6];
  //   RD_H = E_Controls[7]; RD_Opnd = E_Controls[8]; Fetch_1 = in_1; Fetch_2 = in_2; Fetch_3 = in_3

  // Notes on the sheet:
  //   contents of uCode (hex, n*v repeats v):
  //   8*0 101 102 104 108 4*0 11 21 41 81 12 22 42 82 14 24 44 84 18 28 48 88
  //   contents of Program_Memory (hex, n*v repeats v):
  //   8 5 9 7 19 1c
  //   imm a, 5
  //   imm b, 7
  //   mov b, c
  //   mov a, d
  //   IMM -- 000010dd #imm
  //   MOV -- 0001ddss
endmodule
