// Logisim project PFC_mini_74xx.circ as structural Verilog: 14 circuits, main circuit main
module main (
  input  Reset
);

  wire Addr_opnd, ALU_Cin, ALU_inv_B, alu_module_1_cf_out, alu_module_1_nf_out, alu_module_1_zf_out, ALU_s0,
       ALU_s1, ALU_sel_adder, ALU_shr, and_1_out, and_2_out, and_3_out, clock_3_out, clock_5_out,
       clock_6_out, decoder_1_out0, decoder_1_out1, decoder_1_out2, decoder_1_out3, decoder_1_out4,
       decoder_1_out5, decoder_1_out6, decoder_1_out7, decoder_2_out0, decoder_2_out1, decoder_2_out2,
       decoder_2_out3, decoder_2_out4, decoder_2_out5, decoder_2_out6, decoder_2_out7, Execute_1, Execute_2,
       Fetch_1, Fetch_2, Halt, Inc_PC, MMIO, n7400_1_pin5, n7402_1_pin1, n7402_1_pin12, n7402_1_pin13,
       n7408_1_pin12, n7430_1_pin11, n7430_1_pin12, n7432_1_pin3, n7432_1_pin6, n7432_1_pin8, n7432_1_pin11,
       n74139_1_pin1, n74139_1_pin15, n74139_2_pin1, n74161_1_pin2, n74161_1_pin7, n74161_1_pin9,
       n74161_1_pin10, n74541_1_pin19, n74541_2_pin19, n74541_3_pin19, n74541_4_pin19, n_ALU_en, n_Execute_1,
       n_Execute_2, n_Fetch_1, n_Fetch_2, n_In_0_En, n_In_1_En, n_In_2_En, n_In_3_En, n_Jump_en, n_MMIO,
       n_RAM_CS, n_RAM_OE, n_RAM_WE, n_RD_A, n_RD_B, n_RD_C, n_RD_D, n_RD_opnd, n_Reset, n_WR_A, n_WR_B,
       n_WR_C, n_WR_D, nor_1_out, not_1_out, not_2_out, not_3_out, not_4_out, not_5_out, not_14_out,
       not_15_out, not_16_out, not_17_out, or_1_out, random_1_p2;
  wire [1:0] CPU_state;
  wire [2:0] Status_flags;
  wire [3:0] bin_to_bcd_16_1_out_1, bin_to_bcd_16_1_out_10, bin_to_bcd_16_1_out_100,
       bin_to_bcd_16_1_out_1000, bin_to_bcd_16_1_out_10000, Buttons;
  wire [7:0] A_reg_out, Address_bus, alu_module_1_result, B, buffer_1_out, C_reg_out, D_reg_out, Data_bus,
       In_0, In_1, In_2, In_3, led_matrix_emulator_1_row_0, led_matrix_emulator_1_row_1,
       led_matrix_emulator_1_row_2, led_matrix_emulator_1_row_3, led_matrix_emulator_1_row_4,
       led_matrix_emulator_1_row_5, led_matrix_emulator_1_row_6, led_matrix_emulator_1_row_7, MAR_reg_out,
       mux_2_to_1_8_bit_module_1_y, not_6_out, Opcode, Operand, PC_pc_out, Program_out, register_2_q;
  wire [7:6] uCode_ROM_3_data;
  wire [15:0] register_3_q;

  _74161 u_74161_1 (
    .pin1(n_Reset), .pin2(n74161_1_pin2), .pin7(n74161_1_pin7), .pin14(CPU_state[0]), .pin13(CPU_state[1]),
    .pin10(n74161_1_pin10), .pin9(n74161_1_pin9));  // open: pin3, pin4, pin5, pin6, pin15, pin12, pin11
  ROM #(.addrWidth(13)) uCode_ROM_1 (
    .addr({CPU_state, Status_flags, Opcode}),
    .data({n_RAM_WE, n_WR_D, n_WR_C, n_WR_B, n_WR_A, Halt, n_Jump_en, Inc_PC}));
  ROM #(.addrWidth(13)) uCode_ROM_2 (
    .addr({CPU_state, Status_flags, Opcode}),
    .data({n_ALU_en, Addr_opnd, n_RD_opnd, n_RAM_OE, n_RD_D, n_RD_C, n_RD_B, n_RD_A}));
  ROM #(.addrWidth(13)) uCode_ROM_3 (
    .addr({CPU_state, Status_flags, Opcode}),
    .data({uCode_ROM_3_data, ALU_shr, ALU_s1, ALU_s0, ALU_sel_adder, ALU_inv_B, ALU_Cin}));
  _7402 u_7402_1 (
    .pin1(n7402_1_pin1), .pin2(Reset), .pin3(Reset), .pin13(n7402_1_pin13), .pin12(n7402_1_pin12),
    .pin11(Halt), .pin10(n7402_1_pin12), .pin9(n7402_1_pin13), .pin8(Reset));  // open: pin4, pin5, pin6
  _74139 u_74139_1 (
    .pin1(n74139_1_pin1), .pin15(n74139_1_pin15), .pin14(CPU_state[0]), .pin13(CPU_state[1]),
    .pin12(n_Fetch_1), .pin11(n_Fetch_2), .pin10(n_Execute_1), .pin9(n_Execute_2));  // open: pin2, pin3, pin4, pin5, pin6, pin7
  _7408 u_7408_1 (
    .pin13(n7402_1_pin13), .pin12(n7408_1_pin12), .pin11(n74161_1_pin2));  // open: pin1, pin2, pin3, pin4, pin5, pin6, pin10, pin9, pin8
  Clock clock_1 (.out(n7408_1_pin12));
  PC_Module PC (
    .Jump_addr(Operand), .CLK(n74161_1_pin2), .Count_en(Inc_PC), .n_Reset(n7402_1_pin1),
    .n_Jump_en(n_Jump_en), .PC_out(PC_pc_out));
  Register_Module u_Opcode (
    .n_Write_en(n_Fetch_1), .CLK(n74161_1_pin2), .Reset(Reset), .Data_in(Program_out), .Reg_out(Opcode));
  Register_Module u_Operand (
    .n_Write_en(n_Fetch_2), .CLK(n74161_1_pin2), .Reset(Reset), .Data_in(Program_out), .Reg_out(Operand));
  Register_Module A (
    .n_Write_en(n_WR_A), .CLK(n74161_1_pin2), .Reset(Reset), .Data_in(mux_2_to_1_8_bit_module_1_y),
    .Reg_out(A_reg_out));
  Register_Module u_B (.n_Write_en(n_WR_B), .CLK(n74161_1_pin2), .Reset(Reset), .Data_in(Data_bus), .Reg_out(B));
  Register_Module C (.n_Write_en(n_WR_C), .CLK(n74161_1_pin2), .Reset(Reset), .Data_in(Data_bus), .Reg_out(C_reg_out));
  Register_Module D (.n_Write_en(n_WR_D), .CLK(n74161_1_pin2), .Reset(Reset), .Data_in(Data_bus), .Reg_out(D_reg_out));
  ROM Program_Memory (.addr(PC_pc_out), .data(Program_out));
  Tri_state_Module tri_state_module_1 (.n_Enable(n_RD_opnd), .Data_in(Operand), .Data_out(Data_bus));
  Tri_state_Module tri_state_module_2 (.n_Enable(n_RD_A), .Data_in(A_reg_out), .Data_out(Data_bus));
  Tri_state_Module tri_state_module_3 (.n_Enable(n_RD_B), .Data_in(B), .Data_out(Data_bus));
  Tri_state_Module tri_state_module_4 (.n_Enable(n_RD_C), .Data_in(C_reg_out), .Data_out(Data_bus));
  Tri_state_Module tri_state_module_5 (.n_Enable(n_RD_D), .Data_in(D_reg_out), .Data_out(Data_bus));
  Mux_2_to_1_8_bit_Module mux_2_to_1_8_bit_module_1 (
    .B(Data_bus), .Sel(n_ALU_en), .A(alu_module_1_result), .Y(mux_2_to_1_8_bit_module_1_y));
  Mux_2_to_1_8_bit_Module mux_2_to_1_8_bit_module_2 (.B(Operand), .Sel(Addr_opnd), .A(B), .Y(Address_bus));
  Pull_Resistor pull_resistor_1 (.node(Data_bus));
  _7432 u_7432_1 (
    .pin1(n_In_2_En), .pin2(n_RAM_OE), .pin3(n7432_1_pin3), .pin4(n_In_3_En), .pin5(n_RAM_OE),
    .pin6(n7432_1_pin6), .pin13(n_In_0_En), .pin12(n_RAM_OE), .pin11(n7432_1_pin11), .pin10(n_In_1_En),
    .pin9(n_RAM_OE), .pin8(n7432_1_pin8));
  Register_Module MAR (
    .n_Write_en(n_Execute_1), .CLK(n74161_1_pin2), .Reset(Reset), .Data_in(Address_bus), .Reg_out(MAR_reg_out));
  ALU_Module alu_module_1 (
    .Cin(ALU_Cin), .Inv_B(ALU_inv_B), .Sel_adder(ALU_sel_adder), .S0(ALU_s0), .S1(ALU_s1), .SHR(ALU_shr),
    .A(A_reg_out), .B(Data_bus), .Result(alu_module_1_result), .ZF_out(alu_module_1_zf_out),
    .NF_out(alu_module_1_nf_out), .CF_out(alu_module_1_cf_out));
  not not_1 (not_1_out, n_RAM_WE);
  not not_2 (not_2_out, n_RAM_OE);
  not not_3 (not_3_out, n_RAM_CS);
  TTL_74173 ttl_74173_1 (
    .M(1'b0), .N(1'b0), .nG2(1'b0), .nG1(n_ALU_en), .CLK(n74161_1_pin2), .D1(alu_module_1_zf_out),
    .D2(alu_module_1_nf_out), .D3(alu_module_1_cf_out), .D4(1'b0), .CLR(Reset), .Q1(Status_flags[0]),
    .Q2(Status_flags[1]), .Q3(Status_flags[2]));  // open: Q4
  RAM #(.databus("bidir"), .enables("line"), .trigger("high")) Data_Memory (
    .addr(MAR_reg_out), .data(Data_bus));  // open: we, oe, clk
  and and_1 (and_1_out, not_2_out, not_3_out);
  _7430 u_7430_1 (
    .pin1(MAR_reg_out[2]), .pin2(MAR_reg_out[3]), .pin3(MAR_reg_out[4]), .pin4(MAR_reg_out[5]),
    .pin5(MAR_reg_out[6]), .pin6(MAR_reg_out[7]), .pin12(n7430_1_pin12), .pin11(n7430_1_pin11), .pin8(n_MMIO));  // open: pin13, pin10, pin9
  _74541 u_74541_1 (
    .pin1(n7432_1_pin11), .pin2(In_0[0]), .pin3(In_0[1]), .pin4(In_0[2]), .pin5(In_0[3]), .pin6(In_0[4]),
    .pin7(In_0[5]), .pin8(In_0[6]), .pin9(In_0[7]), .pin19(n74541_1_pin19), .pin18(Data_bus[0]),
    .pin17(Data_bus[1]), .pin16(Data_bus[2]), .pin15(Data_bus[3]), .pin14(Data_bus[4]), .pin13(Data_bus[5]),
    .pin12(Data_bus[6]), .pin11(Data_bus[7]));
  _74541 u_74541_2 (
    .pin1(n7432_1_pin8), .pin2(In_1[0]), .pin3(In_1[1]), .pin4(In_1[2]), .pin5(In_1[3]), .pin6(In_1[4]),
    .pin7(In_1[5]), .pin8(In_1[6]), .pin9(In_1[7]), .pin19(n74541_2_pin19), .pin18(Data_bus[0]),
    .pin17(Data_bus[1]), .pin16(Data_bus[2]), .pin15(Data_bus[3]), .pin14(Data_bus[4]), .pin13(Data_bus[5]),
    .pin12(Data_bus[6]), .pin11(Data_bus[7]));
  _74541 u_74541_3 (
    .pin1(n7432_1_pin3), .pin2(In_2[0]), .pin3(In_2[1]), .pin4(In_2[2]), .pin5(In_2[3]), .pin6(In_2[4]),
    .pin7(In_2[5]), .pin8(In_2[6]), .pin9(In_2[7]), .pin19(n74541_3_pin19), .pin18(Data_bus[0]),
    .pin17(Data_bus[1]), .pin16(Data_bus[2]), .pin15(Data_bus[3]), .pin14(Data_bus[4]), .pin13(Data_bus[5]),
    .pin12(Data_bus[6]), .pin11(Data_bus[7]));
  _74541 u_74541_4 (
    .pin1(n7432_1_pin6), .pin2(In_3[0]), .pin3(In_3[1]), .pin4(In_3[2]), .pin5(In_3[3]), .pin6(In_3[4]),
    .pin7(In_3[5]), .pin8(In_3[6]), .pin9(In_3[7]), .pin19(n74541_4_pin19), .pin18(Data_bus[0]),
    .pin17(Data_bus[1]), .pin16(Data_bus[2]), .pin15(Data_bus[3]), .pin14(Data_bus[4]), .pin13(Data_bus[5]),
    .pin12(Data_bus[6]), .pin11(Data_bus[7]));
  _7400 u_7400_1 (
    .pin4(n_MMIO), .pin5(n7400_1_pin5), .pin6(n_RAM_CS), .pin13(n_MMIO), .pin12(n_MMIO), .pin11(MMIO),
    .pin10(n74161_1_pin2), .pin9(n74161_1_pin2), .pin8(n7400_1_pin5));  // open: pin1, pin2, pin3
  _74139 u_74139_2 (
    .pin1(n74139_2_pin1), .pin15(n_MMIO), .pin14(MAR_reg_out[0]), .pin13(MAR_reg_out[1]), .pin12(n_In_0_En),
    .pin11(n_In_1_En), .pin10(n_In_2_En), .pin9(n_In_3_En));  // open: pin2, pin3, pin4, pin5, pin6, pin7
  nor nor_1 (nor_1_out, n_In_2_En, n_RAM_WE);
  _7400 u_7400_2 (.pin6(n_RAM_WE));  // open: pin1, pin2, pin3, pin4, pin5, pin13, pin12, pin11, pin10, pin9, pin8
  Clock clock_2 ();  // open: out
  not not_4 (not_4_out, nor_1_out);
  not not_5 (not_5_out, not_4_out);
  buf buffer_1 (buffer_1_out[0], decoder_1_out0);
  buf buffer_2 (buffer_1_out[1], decoder_1_out1);
  buf buffer_3 (buffer_1_out[2], decoder_1_out2);
  buf buffer_4 (buffer_1_out[3], decoder_1_out3);
  buf buffer_5 (buffer_1_out[4], decoder_1_out4);
  buf buffer_6 (buffer_1_out[5], decoder_1_out5);
  buf buffer_7 (buffer_1_out[6], decoder_1_out6);
  buf buffer_8 (buffer_1_out[7], decoder_1_out7);
  LED_Matrix_Emulator led_matrix_emulator_1 (
    .Row(buffer_1_out), .Column(not_6_out), .Row_0(led_matrix_emulator_1_row_0),
    .Row_1(led_matrix_emulator_1_row_1), .Row_2(led_matrix_emulator_1_row_2),
    .Row_3(led_matrix_emulator_1_row_3), .Row_4(led_matrix_emulator_1_row_4),
    .Row_5(led_matrix_emulator_1_row_5), .Row_6(led_matrix_emulator_1_row_6),
    .Row_7(led_matrix_emulator_1_row_7));
  Decoder #(.select(3)) decoder_1 (
    .out0(decoder_1_out0), .out1(decoder_1_out1), .out2(decoder_1_out2), .out3(decoder_1_out3),
    .out4(decoder_1_out4), .out5(decoder_1_out5), .out6(decoder_1_out6), .out7(decoder_1_out7),
    .sel(Data_bus[5:3]), .en(not_5_out));
  not not_6 (not_6_out[0], decoder_2_out0);
  not not_7 (not_6_out[1], decoder_2_out1);
  not not_8 (not_6_out[2], decoder_2_out2);
  not not_9 (not_6_out[3], decoder_2_out3);
  not not_10 (not_6_out[4], decoder_2_out4);
  not not_11 (not_6_out[5], decoder_2_out5);
  not not_12 (not_6_out[6], decoder_2_out6);
  not not_13 (not_6_out[7], decoder_2_out7);
  Decoder #(.select(3)) decoder_2 (
    .out0(decoder_2_out0), .out1(decoder_2_out1), .out2(decoder_2_out2), .out3(decoder_2_out3),
    .out4(decoder_2_out4), .out5(decoder_2_out5), .out6(decoder_2_out6), .out7(decoder_2_out7),
    .sel(Data_bus[2:0]), .en(not_5_out));
  LED led_1 (.in(Fetch_1));
  LED led_2 (.in(Fetch_2));
  LED led_3 (.in(Execute_1));
  LED led_4 (.in(Execute_2));
  DotMatrix #(.dotshape("circle"), .inputtype("row"), .matrixcols(8), .matrixrows(8), .persist(6000)) dotmatrix_1 (
    .row0(led_matrix_emulator_1_row_0), .row1(led_matrix_emulator_1_row_1),
    .row2(led_matrix_emulator_1_row_2), .row3(led_matrix_emulator_1_row_3),
    .row4(led_matrix_emulator_1_row_4), .row5(led_matrix_emulator_1_row_5),
    .row6(led_matrix_emulator_1_row_6), .row7(led_matrix_emulator_1_row_7));
  Button button_1 (.out(Buttons[3]));
  Button button_2 (.out(Buttons[1]));
  Register #(.width(4)) register_1 (.D(Buttons), .en(or_1_out), .clk(clock_3_out), .Q(In_0[3:0]), .clr(Reset));
  or or_1 (or_1_out, Buttons[0], Buttons[1], Buttons[2], Buttons[3]);
  Clock clock_3 (.out(clock_3_out));
  Button button_3 (.out(Buttons[0]));
  Button button_4 (.out(Buttons[2]));
  // Random random_1: pin names not known; wires that end beside it: 1'b1, random_1_p2
  Clock clock_4 (.out(random_1_p2));
  _7404 u_7404_1 (
    .pin1(n_Execute_1), .pin2(Execute_1), .pin3(n_Execute_2), .pin4(Execute_2), .pin13(n_Fetch_2),
    .pin12(Fetch_2), .pin11(n_Fetch_1), .pin10(Fetch_1));  // open: pin5, pin6, pin9, pin8
  Hex_Digit_Display hex_digit_display_1 (.value(bin_to_bcd_16_1_out_10000));  // open: dp
  Hex_Digit_Display hex_digit_display_2 (.value(bin_to_bcd_16_1_out_1000));  // open: dp
  Hex_Digit_Display hex_digit_display_3 (.value(bin_to_bcd_16_1_out_100));  // open: dp
  Bin_to_BCD_16 bin_to_bcd_16_1 (
    .Bin(register_3_q), .Out_1(bin_to_bcd_16_1_out_1), .Out_10(bin_to_bcd_16_1_out_10),
    .Out_100(bin_to_bcd_16_1_out_100), .Out_1000(bin_to_bcd_16_1_out_1000),
    .Out_10000(bin_to_bcd_16_1_out_10000));
  Register register_2 (.D(Data_bus), .en(and_2_out), .clk(clock_5_out), .Q(register_2_q));  // open: clr
  not not_14 (not_14_out, n_RAM_WE);
  and and_2 (and_2_out, not_14_out, not_15_out);
  not not_15 (not_15_out, n_In_0_En);
  Clock clock_5 (.out(clock_5_out));
  not not_16 (not_16_out, n_RAM_WE);
  and and_3 (and_3_out, not_16_out, not_17_out);
  not not_17 (not_17_out, n_In_1_En);
  Hex_Digit_Display hex_digit_display_4 (.value(bin_to_bcd_16_1_out_10));  // open: dp
  Hex_Digit_Display hex_digit_display_5 (.value(bin_to_bcd_16_1_out_1));  // open: dp
  Register #(.width(16)) register_3 (
    .D({Data_bus, register_2_q}), .en(and_3_out), .clk(clock_6_out), .Q(register_3_q));  // open: clr
  Clock clock_6 (.out(clock_6_out));
  // also tied to GND on the sheet: {n74139_1_pin1, n74139_1_pin15, n74541_1_pin19, n74541_2_pin19, n74541_3_pin19, n74541_4_pin19, n74139_2_pin1, In_0[4], In_0[5], In_0[6], In_0[7]}
  // also tied to VCC on the sheet: {n74161_1_pin10, n74161_1_pin7, n74161_1_pin9, n7430_1_pin12, n7430_1_pin11}

  // Other names for the same wires on the sheet: n_WR_mem = n_RAM_WE; n_RD_mem = n_RAM_OE

  // Notes on the sheet:
  //   contents of uCode_ROM_1 (hex, n*v repeats v):
  //   2048*fb 16*fa 16*fb 4*fa 4*fb 4*fa 4*fb 4*fa 4*fb 4*fa 4*fb 4*fa 4*fb 4*fa 4*fb 4*fa 4*fb 4*fa 20*fb
  //   20*fa 4*fb 4*fa 4*fb 4*fa 4*fb 4*fa 4*fb 4*fa 4*fb 4*fa 4*fb 4*fa 4*fb 4*fa 4*fb 4*fa 4*fb 4*fa 4*fb
  //   4*fa 4*fb 4*fa 4*fb 4*fa 4*fb 4*fa 4*fb 4*fa 4*fb 4*fa 4*fb 16*fa 16*fb 4*fa 4*fb 4*fa 4*fb 4*fa
  //   4*fb 4*fa 4*fb 4*fa 4*fb 4*fa 4*fb 4*fa 4*fb 4*fa 20*fb 20*fa 4*fb 4*fa 4*fb 4*fa 4*fb 4*fa 4*fb
  //   4*fa 4*fb 4*fa 4*fb 4*fa 4*fb 4*fa 4*fb 4*fa 4*fb 4*fa 4*fb 4*fa 4*fb 4*fa 4*fb 4*fa 4*fb 4*fa 4*fb
  //   4*fa 4*fb 4*fa 4*fb 16*fa 16*fb 4*fa 4*fb 4*fa 4*fb 4*fa 4*fb 4*fa 4*fb 4*fa 4*fb 4*fa 4*fb 4*fa
  //   4*fb 4*fa 20*fb 20*fa 4*fb 4*fa 4*fb 4*fa 4*fb 4*fa 4*fb 4*fa 4*fb 4*fa 4*fb 4*fa 4*fb 4*fa 4*fb
  //   4*fa 4*fb 4*fa 4*fb 4*fa 4*fb 4*fa 4*fb 4*fa 4*fb 4*fa 4*fb 4*fa 4*fb 4*fa 4*fb 16*fa 16*fb 4*fa
  //   4*fb 4*fa 4*fb 4*fa 4*fb 4*fa 4*fb 4*fa 4*fb 4*fa 4*fb 4*fa 4*fb 4*fa 20*fb 20*fa 4*fb 4*fa 4*fb
  //   4*fa 4*fb 4*fa 4*fb 4*fa 4*fb 4*fa 4*fb 4*fa 4*fb 4*fa 4*fb 4*fa 4*fb 4*fa 4*fb 4*fa 4*fb 4*fa 4*fb
  //   4*fa 4*fb 4*fa 4*fb 4*fa 4*fb 4*fa 4*fb 16*fa 16*fb 4*fa 4*fb 4*fa 4*fb 4*fa 4*fb 4*fa 4*fb 4*fa
  //   4*fb 4*fa 4*fb 4*fa 4*fb 4*fa 20*fb 20*fa 4*fb 4*fa 4*fb 4*fa 4*fb 4*fa 4*fb 4*fa 4*fb 4*fa 4*fb
  //   4*fa 4*fb 4*fa 4*fb 4*fa 4*fb 4*fa 4*fb 4*fa 4*fb 4*fa 4*fb 4*fa 4*fb 4*fa 4*fb 4*fa 4*fb 4*fa 4*fb
  //   16*fa 16*fb 4*fa 4*fb 4*fa 4*fb 4*fa 4*fb 4*fa 4*fb 4*fa 4*fb 4*fa 4*fb 4*fa 4*fb 4*fa 20*fb 20*fa
  //   4*fb 4*fa 4*fb 4*fa 4*fb 4*fa 4*fb 4*fa 4*fb 4*fa 4*fb 4*fa 4*fb 4*fa 4*fb 4*fa 4*fb 4*fa 4*fb 4*fa
  //   4*fb 4*fa 4*fb 4*fa 4*fb 4*fa 4*fb 4*fa 4*fb 4*fa 4*fb 16*fa 16*fb 4*fa 4*fb 4*fa 4*fb 4*fa 4*fb
  //   4*fa 4*fb 4*fa 4*fb 4*fa 4*fb 4*fa 4*fb 4*fa 20*fb 20*fa 4*fb 4*fa 4*fb 4*fa 4*fb 4*fa 4*fb 4*fa
  //   4*fb 4*fa 4*fb 4*fa 4*fb 4*fa 4*fb 4*fa 4*fb 4*fa 4*fb 4*fa 4*fb 4*fa 4*fb 4*fa 4*fb 4*fa 4*fb 4*fa
  //   4*fb 4*fa 4*fb 16*fa 16*fb 4*fa 4*fb 4*fa 4*fb 4*fa 4*fb 4*fa 4*fb 4*fa 4*fb 4*fa 4*fb 4*fa 4*fb
  //   4*fa 20*fb 20*fa 4*fb 4*fa 4*fb 4*fa 4*fb 4*fa 4*fb 4*fa 4*fb 4*fa 4*fb 4*fa 4*fb 4*fa 4*fb 4*fa
  //   4*fb 4*fa 4*fb 4*fa 4*fb 4*fa 4*fb 4*fa 4*fb 4*fa 4*fb 4*fa 4*fb 4*fa 4*fb 2048*fa 4*f2 4*ea 4*da
  //   4*ba f2 ea da ba f2 ea da ba f2 ea da ba f2 ea da ba 16*7a f2 ea da ba f2 ea da ba f2 ea da ba f2 ea
  //   da ba 32*fa 8*f8 4*fa 4*f8 16*fe 132*f2 4*ea 4*da 4*ba f2 ea da ba f2 ea da ba f2 ea da ba f2 ea da
  //   ba 16*7a f2 ea da ba f2 ea da ba f2 ea da ba f2 ea da ba 32*fa 9*f8 fa fa f8 fa f8 f8 fa 16*fe
  //   132*f2 4*ea 4*da 4*ba f2 ea da ba f2 ea da ba f2 ea da ba f2 ea da ba 16*7a f2 ea da ba f2 ea da ba
  //   f2 ea da ba f2 ea da ba 32*fa 8*f8 fa f8 fa f8 f8 fa f8 fa 16*fe 132*f2 4*ea 4*da 4*ba f2 ea da ba
  //   f2 ea da ba f2 ea da ba f2 ea da ba 16*7a f2 ea da ba f2 ea da ba f2 ea da ba f2 ea da ba 32*fa
  //   10*f8 fa f8 fa fa f8 fa 16*fe 132*f2 4*ea 4*da 4*ba f2 ea da ba f2 ea da ba f2 ea da ba f2 ea da ba
  //   16*7a f2 ea da ba f2 ea da ba f2 ea da ba f2 ea da ba 32*fa 8*f8 fa fa f8 fa f8 f8 fa f8 16*fe
  //   132*f2 4*ea 4*da 4*ba f2 ea da ba f2 ea da ba f2 ea da ba f2 ea da ba 16*7a f2 ea da ba f2 ea da ba
  //   f2 ea da ba f2 ea da ba 32*fa 9*f8 fa f8 f8 fa f8 fa fa 16*fe 132*f2 4*ea 4*da 4*ba f2 ea da ba f2
  //   ea da ba f2 ea da ba f2 ea da ba 16*7a f2 ea da ba f2 ea da ba f2 ea da ba f2 ea da ba 32*fa 8*f8 fa
  //   4*f8 fa fa fa 16*fe 132*f2 4*ea 4*da 4*ba f2 ea da ba f2 ea da ba f2 ea da ba f2 ea da ba 16*7a f2
  //   ea da ba f2 ea da ba f2 ea da ba f2 ea da ba 32*fa 12*f8 4*fa 16*fe 128*f2
  //   contents of uCode_ROM_2 (hex, n*v repeats v):
  //   4132*bf 4*ff 4*bf 4*ff 4*bf 4*ff 4*bf 4*ff 228*bf 4*ff 4*bf 4*ff 4*bf 4*ff 4*bf 4*ff 228*bf 4*ff
  //   4*bf 4*ff 4*bf 4*ff 4*bf 4*ff 228*bf 4*ff 4*bf 4*ff 4*bf 4*ff 4*bf 4*ff 228*bf 4*ff 4*bf 4*ff 4*bf
  //   4*ff 4*bf 4*ff 228*bf 4*ff 4*bf 4*ff 4*bf 4*ff 4*bf 4*ff 228*bf 4*ff 4*bf 4*ff 4*bf 4*ff 4*bf 4*ff
  //   228*bf 4*ff 4*bf 4*ff 4*bf 4*ff 4*bf 4*ff 192*bf be bd bb b7 be bd bb b7 be bd bb b7 be bd bb b7
  //   16*9f be bd bb b7 be bd bb b7 be bd bb b7 be bd bb b7 16*af 3e 3d 3b 37 4*1f 3e 3d 3b 37 4*1f 3e 3d
  //   3b 37 4*1f 3e 3d 3b 37 4*1f 32*bf 3e 3d 3b 37 4*1f 3e 3d 3b 37 4*1f 3e 3d 3b 37 4*1f 3e 3d 3b 37
  //   4*1f 3e 3d 3b 37 4*1f 3e 3d 3b 37 4*1f 3e 3d 3b 37 4*1f 3e 3d 3b 37 4*1f 3e 3d 3b 37 4*1f 3e 3d 3b
  //   37 4*1f 3e 3d 3b 37 4*1f 3e 3d 3b 37 4*1f 3e 3d 3b 37 4*1f 3e 3d 3b 37 4*1f 3e 3d 3b 37 3e 3d 3b 37
  //   3e 3d 3b 37 3e 3d 3b 37 be bd bb b7 be bd bb b7 be bd bb b7 be bd bb b7 16*9f be bd bb b7 be bd bb
  //   b7 be bd bb b7 be bd bb b7 16*af 3e 3d 3b 37 4*1f 3e 3d 3b 37 4*1f 3e 3d 3b 37 4*1f 3e 3d 3b 37 4*1f
  //   32*bf 3e 3d 3b 37 4*1f 3e 3d 3b 37 4*1f 3e 3d 3b 37 4*1f 3e 3d 3b 37 4*1f 3e 3d 3b 37 4*1f 3e 3d 3b
  //   37 4*1f 3e 3d 3b 37 4*1f 3e 3d 3b 37 4*1f 3e 3d 3b 37 4*1f 3e 3d 3b 37 4*1f 3e 3d 3b 37 4*1f 3e 3d
  //   3b 37 4*1f 3e 3d 3b 37 4*1f 3e 3d 3b 37 4*1f 3e 3d 3b 37 3e 3d 3b 37 3e 3d 3b 37 3e 3d 3b 37 be bd
  //   bb b7 be bd bb b7 be bd bb b7 be bd bb b7 16*9f be bd bb b7 be bd bb b7 be bd bb b7 be bd bb b7
  //   16*af 3e 3d 3b 37 4*1f 3e 3d 3b 37 4*1f 3e 3d 3b 37 4*1f 3e 3d 3b 37 4*1f 32*bf 3e 3d 3b 37 4*1f 3e
  //   3d 3b 37 4*1f 3e 3d 3b 37 4*1f 3e 3d 3b 37 4*1f 3e 3d 3b 37 4*1f 3e 3d 3b 37 4*1f 3e 3d 3b 37 4*1f
  //   3e 3d 3b 37 4*1f 3e 3d 3b 37 4*1f 3e 3d 3b 37 4*1f 3e 3d 3b 37 4*1f 3e 3d 3b 37 4*1f 3e 3d 3b 37
  //   4*1f 3e 3d 3b 37 4*1f 3e 3d 3b 37 3e 3d 3b 37 3e 3d 3b 37 3e 3d 3b 37 be bd bb b7 be bd bb b7 be bd
  //   bb b7 be bd bb b7 16*9f be bd bb b7 be bd bb b7 be bd bb b7 be bd bb b7 16*af 3e 3d 3b 37 4*1f 3e 3d
  //   3b 37 4*1f 3e 3d 3b 37 4*1f 3e 3d 3b 37 4*1f 32*bf 3e 3d 3b 37 4*1f 3e 3d 3b 37 4*1f 3e 3d 3b 37
  //   4*1f 3e 3d 3b 37 4*1f 3e 3d 3b 37 4*1f 3e 3d 3b 37 4*1f 3e 3d 3b 37 4*1f 3e 3d 3b 37 4*1f 3e 3d 3b
  //   37 4*1f 3e 3d 3b 37 4*1f 3e 3d 3b 37 4*1f 3e 3d 3b 37 4*1f 3e 3d 3b 37 4*1f 3e 3d 3b 37 4*1f 3e 3d
  //   3b 37 3e 3d 3b 37 3e 3d 3b 37 3e 3d 3b 37 be bd bb b7 be bd bb b7 be bd bb b7 be bd bb b7 16*9f be
  //   bd bb b7 be bd bb b7 be bd bb b7 be bd bb b7 16*af 3e 3d 3b 37 4*1f 3e 3d 3b 37 4*1f 3e 3d 3b 37
  //   4*1f 3e 3d 3b 37 4*1f 32*bf 3e 3d 3b 37 4*1f 3e 3d 3b 37 4*1f 3e 3d 3b 37 4*1f 3e 3d 3b 37 4*1f 3e
  //   3d 3b 37 4*1f 3e 3d 3b 37 4*1f 3e 3d 3b 37 4*1f 3e 3d 3b 37 4*1f 3e 3d 3b 37 4*1f 3e 3d 3b 37 4*1f
  //   3e 3d 3b 37 4*1f 3e 3d 3b 37 4*1f 3e 3d 3b 37 4*1f 3e 3d 3b 37 4*1f 3e 3d 3b 37 3e 3d 3b 37 3e 3d 3b
  //   37 3e 3d 3b 37 be bd bb b7 be bd bb b7 be bd bb b7 be bd bb b7 16*9f be bd bb b7 be bd bb b7 be bd
  //   bb b7 be bd bb b7 16*af 3e 3d 3b 37 4*1f 3e 3d 3b 37 4*1f 3e 3d 3b 37 4*1f 3e 3d 3b 37 4*1f 32*bf 3e
  //   3d 3b 37 4*1f 3e 3d 3b 37 4*1f 3e 3d 3b 37 4*1f 3e 3d 3b 37 4*1f 3e 3d 3b 37 4*1f 3e 3d 3b 37 4*1f
  //   3e 3d 3b 37 4*1f 3e 3d 3b 37 4*1f 3e 3d 3b 37 4*1f 3e 3d 3b 37 4*1f 3e 3d 3b 37 4*1f 3e 3d 3b 37
  //   4*1f 3e 3d 3b 37 4*1f 3e 3d 3b 37 4*1f 3e 3d 3b 37 3e 3d 3b 37 3e 3d 3b 37 3e 3d 3b 37 be bd bb b7
  //   be bd bb b7 be bd bb b7 be bd bb b7 16*9f be bd bb b7 be bd bb b7 be bd bb b7 be bd bb b7 16*af 3e
  //   3d 3b 37 4*1f 3e 3d 3b 37 4*1f 3e 3d 3b 37 4*1f 3e 3d 3b 37 4*1f 32*bf 3e 3d 3b 37 4*1f 3e 3d 3b 37
  //   4*1f 3e 3d 3b 37 4*1f 3e 3d 3b 37 4*1f 3e 3d 3b 37 4*1f 3e 3d 3b 37 4*1f 3e 3d 3b 37 4*1f 3e 3d 3b
  //   37 4*1f 3e 3d 3b 37 4*1f 3e 3d 3b 37 4*1f 3e 3d 3b 37 4*1f 3e 3d 3b 37 4*1f 3e 3d 3b 37 4*1f 3e 3d
  //   3b 37 4*1f 3e 3d 3b 37 3e 3d 3b 37 3e 3d 3b 37 3e 3d 3b 37 be bd bb b7 be bd bb b7 be bd bb b7 be bd
  //   bb b7 16*9f be bd bb b7 be bd bb b7 be bd bb b7 be bd bb b7 16*af 3e 3d 3b 37 4*1f 3e 3d 3b 37 4*1f
  //   3e 3d 3b 37 4*1f 3e 3d 3b 37 4*1f 32*bf 3e 3d 3b 37 4*1f 3e 3d 3b 37 4*1f 3e 3d 3b 37 4*1f 3e 3d 3b
  //   37 4*1f 3e 3d 3b 37 4*1f 3e 3d 3b 37 4*1f 3e 3d 3b 37 4*1f 3e 3d 3b 37 4*1f 3e 3d 3b 37 4*1f 3e 3d
  //   3b 37 4*1f 3e 3d 3b 37 4*1f 3e 3d 3b 37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
  //   contents of uCode_ROM_3 (hex, n*v repeats v):
  //   6208*0 16*7 48*0 16*4 16*7 16*4 16*6 16*0 16*8 16*10 16*38 64*0 16*7 48*0 16*4 16*7 16*4 16*6 16*0
  //   16*8 16*10 16*38 64*0 16*7 48*0 16*4 16*7 16*4 16*6 16*0 16*8 16*10 16*38 64*0 16*7 48*0 16*4 16*7
  //   16*4 16*6 16*0 16*8 16*10 16*38 64*0 16*7 48*0 16*4 16*7 16*5 16*7 16*0 16*8 16*10 16*38 64*0 16*7
  //   48*0 16*4 16*7 16*5 16*7 16*0 16*8 16*10 16*38 64*0 16*7 48*0 16*4 16*7 16*5 16*7 16*0 16*8 16*10
  //   16*38 64*0 16*7 48*0 16*4 16*7 16*5 16*7 16*0 16*8 16*10 16*38
  //   contents of Program_Memory (hex, n*v repeats v):
  //   10 4 24 10 10 40 24 11 10 1b 24 13 34 fd c4 3f 24 12 60 70 34 fc 44 0 68 1c 24 10 34 11 4 32 35 10 1
  //   c4 1 68 2c 2 94 8 60 4b 1 c4 2 68 36 2 84 8 60 4b 1 c4 4 68 40 2 84 1 60 43 2 94 1 c4 7 4 2 c4 38 60
  //   51 c4 38 4 2 c4 7 d1 24 13 35 12 41 6c 61 34 11 84 1 24 11 60 c 10 40 12 1 82 4 33 92 4 23 82 44 7f
  //   6c 65 34 13 35 11 20 1 84 1 8 10 40 4 33 27 fe 84 1 42 69 7b 34 12 24 fe 60 14
endmodule

module Bin_to_BCD_16 (
  input  [15:0] Bin,
  output [3:0] Out_1,
  output [3:0] Out_10,
  output [3:0] Out_100,
  output [3:0] Out_1000,
  output [3:0] Out_10000
);

  wire [15:0] divider_1_out, divider_2_out, divider_3_out, divider_4_out;
  wire [15:4] divider_1_rem, divider_2_rem, divider_3_rem, divider_4_rem, divider_5_rem;

  Divider #(.width(16)) divider_1 (
    .a(Bin), .b(16'ha), .out(divider_1_out), .rem({divider_1_rem, Out_1}));  // open: upper
  Divider #(.width(16)) divider_2 (
    .a(divider_1_out), .b(16'ha), .out(divider_2_out), .rem({divider_2_rem, Out_10}));  // open: upper
  Divider #(.width(16)) divider_3 (
    .a(divider_2_out), .b(16'ha), .out(divider_3_out), .rem({divider_3_rem, Out_100}));  // open: upper
  Divider #(.width(16)) divider_4 (
    .a(divider_3_out), .b(16'ha), .out(divider_4_out), .rem({divider_4_rem, Out_1000}));  // open: upper
  Divider #(.width(16)) divider_5 (.a(divider_4_out), .b(16'ha), .rem({divider_5_rem, Out_10000}));  // open: out, upper
endmodule

module LED_Matrix_Emulator (
  input  [7:0] Row,
  input  [7:0] Column,
  output [7:0] Row_0,
  output [7:0] Row_1,
  output [7:0] Row_2,
  output [7:0] Row_3,
  output [7:0] Row_4,
  output [7:0] Row_5,
  output [7:0] Row_6,
  output [7:0] Row_7
);

  wire [7:0] buffer_1_out, not_1_out;

  assign buffer_1_out = Row;  // Buffer buffer_1, 8 bits wide
  assign not_1_out = ~Column;  // NOT_Gate not_1, 8 bits wide
  assign Row_0 = not_1_out & {8{buffer_1_out[0]}};  // AND_Gate and_1, 8 bits wide
  assign Row_1 = not_1_out & {8{buffer_1_out[1]}};  // AND_Gate and_2, 8 bits wide
  assign Row_2 = not_1_out & {8{buffer_1_out[2]}};  // AND_Gate and_3, 8 bits wide
  assign Row_3 = not_1_out & {8{buffer_1_out[3]}};  // AND_Gate and_4, 8 bits wide
  assign Row_4 = not_1_out & {8{buffer_1_out[4]}};  // AND_Gate and_5, 8 bits wide
  assign Row_5 = not_1_out & {8{buffer_1_out[5]}};  // AND_Gate and_6, 8 bits wide
  assign Row_6 = not_1_out & {8{buffer_1_out[6]}};  // AND_Gate and_7, 8 bits wide
  assign Row_7 = not_1_out & {8{buffer_1_out[7]}};  // AND_Gate and_8, 8 bits wide
endmodule

module TTL_7483 (
  input  B4,
  input  Cin,
  input  B1,
  input  A1,
  input  A4,
  input  A3,
  input  B3,
  input  B2,
  input  A2,
  output S4,
  output Cout,
  output S1,
  output S3,
  output S2
);

  wire adder_2_cout, adder_3_cout, adder_4_cout;

  Adder #(.width(1)) adder_1 (.a(A4), .b(B4), .out(S4), .cin(adder_2_cout), .cout(Cout));
  Adder #(.width(1)) adder_2 (.a(A3), .b(B3), .out(S3), .cin(adder_3_cout), .cout(adder_2_cout));
  Adder #(.width(1)) adder_3 (.a(A2), .b(B2), .out(S2), .cin(adder_4_cout), .cout(adder_3_cout));
  Adder #(.width(1)) adder_4 (.a(A1), .b(B1), .out(S1), .cin(Cin), .cout(adder_4_cout));
endmodule

module TTL_74173 (
  input  M,
  input  N,
  input  nG2,
  input  nG1,
  input  CLK,
  input  D1,
  input  D2,
  input  D3,
  input  D4,
  input  CLR,
  output Q1,
  output Q2,
  output Q3,
  output Q4
);

  wire and_1_out, and_2_out, and_3_out, and_4_out, and_5_out, and_6_out, and_7_out, and_8_out, and_9_out,
       and_10_out, d_ff_1_q, d_ff_1_qn, d_ff_2_q, d_ff_2_qn, d_ff_3_q, d_ff_3_qn, d_ff_4_q, d_ff_4_qn,
       not_1_out, not_2_out, not_3_out, not_4_out, not_5_out, not_6_out, not_7_out, not_8_out, not_9_out,
       not_10_out, not_11_out, not_12_out, not_13_out, not_14_out, not_15_out, or_1_out, or_2_out, or_3_out,
       or_4_out;

  not not_1 (not_1_out, CLK);
  not not_2 (not_2_out, CLR);
  and and_1 (and_1_out, ~M, ~N);  // AND_Gate
  and and_2 (and_2_out, ~nG2, ~nG1);  // AND_Gate
  not not_3 (not_3_out, and_2_out);
  and and_3 (and_3_out, d_ff_1_q, not_3_out);
  and and_4 (and_4_out, D1, and_2_out);
  and and_5 (and_5_out, d_ff_2_q, not_3_out);
  and and_6 (and_6_out, D2, and_2_out);
  and and_7 (and_7_out, d_ff_3_q, not_3_out);
  and and_8 (and_8_out, D3, and_2_out);
  and and_9 (and_9_out, d_ff_4_q, not_3_out);
  and and_10 (and_10_out, D4, and_2_out);
  D_Flip_Flop d_ff_1 (.D(or_1_out), .clk(not_4_out), .Q(d_ff_1_q), .Qn(d_ff_1_qn), .reset(not_5_out));  // open: preset
  or or_1 (or_1_out, and_3_out, and_4_out);
  not not_4 (not_4_out, not_1_out);
  not not_5 (not_5_out, not_2_out);
  D_Flip_Flop d_ff_2 (.D(or_2_out), .clk(not_6_out), .Q(d_ff_2_q), .Qn(d_ff_2_qn), .reset(not_7_out));  // open: preset
  or or_2 (or_2_out, and_5_out, and_6_out);
  not not_6 (not_6_out, not_1_out);
  not not_7 (not_7_out, not_2_out);
  D_Flip_Flop d_ff_3 (.D(or_3_out), .clk(not_8_out), .Q(d_ff_3_q), .Qn(d_ff_3_qn), .reset(not_9_out));  // open: preset
  or or_3 (or_3_out, and_7_out, and_8_out);
  not not_8 (not_8_out, not_1_out);
  not not_9 (not_9_out, not_2_out);
  D_Flip_Flop d_ff_4 (
    .D(or_4_out), .clk(not_10_out), .Q(d_ff_4_q), .Qn(d_ff_4_qn), .reset(not_11_out));  // open: preset
  or or_4 (or_4_out, and_9_out, and_10_out);
  not not_10 (not_10_out, not_1_out);
  not not_11 (not_11_out, not_2_out);
  not not_12 (not_12_out, d_ff_1_qn);
  assign Q1 = and_1_out ? not_12_out : 1'bz;  // Controlled_Buffer controlled_buffer_1
  not not_13 (not_13_out, d_ff_2_qn);
  assign Q2 = and_1_out ? not_13_out : 1'bz;  // Controlled_Buffer controlled_buffer_2
  not not_14 (not_14_out, d_ff_3_qn);
  assign Q3 = and_1_out ? not_14_out : 1'bz;  // Controlled_Buffer controlled_buffer_3
  not not_15 (not_15_out, d_ff_4_qn);
  assign Q4 = and_1_out ? not_15_out : 1'bz;  // Controlled_Buffer controlled_buffer_4
endmodule

module TTL_74175 (
  input  D1,
  input  D2,
  input  D3,
  input  D4,
  input  CLK,
  input  nCLR,
  output Q1,
  output nQ1,
  output Q2,
  output nQ2,
  output Q3,
  output nQ3,
  output Q4,
  output nQ4
);

  wire not_1_out, not_2_out, not_3_out, not_4_out, not_5_out, not_6_out, not_7_out, not_8_out, not_9_out,
       not_10_out, not_11_out;

  not not_1 (not_1_out, CLK);
  not not_2 (not_2_out, nCLR);
  not not_3 (not_3_out, not_2_out);
  D_Flip_Flop d_ff_1 (.D(D1), .clk(not_4_out), .Q(Q1), .Qn(nQ1), .reset(not_5_out));  // open: preset
  not not_4 (not_4_out, not_1_out);
  not not_5 (not_5_out, not_3_out);
  D_Flip_Flop d_ff_2 (.D(D2), .clk(not_6_out), .Q(Q2), .Qn(nQ2), .reset(not_7_out));  // open: preset
  not not_6 (not_6_out, not_1_out);
  not not_7 (not_7_out, not_3_out);
  D_Flip_Flop d_ff_3 (.D(D3), .clk(not_8_out), .Q(Q3), .Qn(nQ3), .reset(not_9_out));  // open: preset
  not not_8 (not_8_out, not_1_out);
  not not_9 (not_9_out, not_3_out);
  D_Flip_Flop d_ff_4 (.D(D4), .clk(not_10_out), .Q(Q4), .Qn(nQ4), .reset(not_11_out));  // open: preset
  not not_10 (not_10_out, not_1_out);
  not not_11 (not_11_out, not_3_out);
endmodule

module Accumulator_Module (
  input  [7:0] Data_in,
  input  n_Write_en,
  input  CLK,
  input  Reset,
  output [7:0] Reg_out
);

  TTL_74173 ttl_74173_1 (
    .M(1'b0), .N(1'b0), .nG2(1'b0), .nG1(n_Write_en), .CLK(CLK), .D1(Data_in[7]), .D2(Data_in[6]),
    .D3(Data_in[5]), .D4(Data_in[4]), .CLR(Reset), .Q1(Reg_out[7]), .Q2(Reg_out[6]), .Q3(Reg_out[5]),
    .Q4(Reg_out[4]));
  TTL_74173 ttl_74173_2 (
    .M(1'b0), .N(1'b0), .nG2(1'b0), .nG1(n_Write_en), .CLK(CLK), .D1(Data_in[3]), .D2(Data_in[2]),
    .D3(Data_in[1]), .D4(Data_in[0]), .CLR(Reset), .Q1(Reg_out[3]), .Q2(Reg_out[2]), .Q3(Reg_out[1]),
    .Q4(Reg_out[0]));
  LED led_1 (.in(Reg_out[7]));
  LED led_2 (.in(Reg_out[6]));
  LED led_3 (.in(Reg_out[5]));
  LED led_4 (.in(Reg_out[4]));
  LED led_5 (.in(Reg_out[3]));
  LED led_6 (.in(Reg_out[2]));
  LED led_7 (.in(Reg_out[1]));
  LED led_8 (.in(Reg_out[0]));
endmodule

module ALU_Module (
  input  Cin,
  input  Inv_B,
  input  Sel_adder,
  input  S0,
  input  S1,
  input  SHR,
  input  [7:0] A,
  input  [7:0] B,
  output [7:0] Result,
  output ZF_out,
  output NF_out,
  output CF_out
);

  wire add0, add1, add2, add3, add4, add5, add6, add7, Adder_Cout, and0, and1, and2, and3, and4, and5, and6,
       and7, Bx0, Bx1, Bx2, Bx3, Bx4, Bx5, Bx6, Bx7, mux0, mux1, mux2, mux3, mux4, mux5, mux6, mux7,
       n7400_1_pin6, n7400_1_pin11, n7402_1_pin1, n7402_1_pin4, n7402_1_pin10, n7402_1_pin13, n7408_3_pin3,
       n7408_3_pin11, n74153_1_pin1, n74153_1_pin15, n74153_2_pin1, n74153_2_pin15, n74153_3_pin1,
       n74153_3_pin15, n74153_4_pin1, n74153_4_pin15, n74157_1_pin15, n74157_2_pin15, n74283_1_pin7, or0,
       or1, or2, or3, or4, or5, or6, or7, shr7, xor0, xor1, xor2, xor3, xor4, xor5, xor6, xor7;

  _7486 u_7486_1 (
    .pin1(B[5]), .pin2(Inv_B), .pin3(Bx5), .pin4(B[4]), .pin5(Inv_B), .pin6(Bx4), .pin13(B[6]),
    .pin12(Inv_B), .pin11(Bx6), .pin10(B[7]), .pin9(Inv_B), .pin8(Bx7));
  _7408 u_7408_1 (
    .pin1(A[5]), .pin2(B[5]), .pin3(and5), .pin4(A[4]), .pin5(B[4]), .pin6(and4), .pin13(A[6]), .pin12(B[6]),
    .pin11(and6), .pin10(A[7]), .pin9(B[7]), .pin8(and7));
  _7486 u_7486_2 (
    .pin1(A[5]), .pin2(B[5]), .pin3(xor5), .pin4(A[4]), .pin5(B[4]), .pin6(xor4), .pin13(A[6]), .pin12(B[6]),
    .pin11(xor6), .pin10(A[7]), .pin9(B[7]), .pin8(xor7));
  _7486 u_7486_3 (
    .pin1(B[1]), .pin2(Inv_B), .pin3(Bx1), .pin4(B[0]), .pin5(Inv_B), .pin6(Bx0), .pin13(B[2]),
    .pin12(Inv_B), .pin11(Bx2), .pin10(B[3]), .pin9(Inv_B), .pin8(Bx3));
  _7408 u_7408_2 (
    .pin1(A[1]), .pin2(B[1]), .pin3(and1), .pin4(A[0]), .pin5(B[0]), .pin6(and0), .pin13(A[2]), .pin12(B[2]),
    .pin11(and2), .pin10(A[3]), .pin9(B[3]), .pin8(and3));
  _7486 u_7486_4 (
    .pin1(A[1]), .pin2(B[1]), .pin3(xor1), .pin4(A[0]), .pin5(B[0]), .pin6(xor0), .pin13(A[2]), .pin12(B[2]),
    .pin11(xor2), .pin10(A[3]), .pin9(B[3]), .pin8(xor3));
  _74283 u_74283_1 (
    .pin1(add5), .pin2(Bx5), .pin3(A[5]), .pin4(add4), .pin5(A[4]), .pin6(Bx4), .pin7(n74283_1_pin7),
    .pin15(Bx6), .pin14(A[6]), .pin13(add6), .pin12(A[7]), .pin11(Bx7), .pin10(add7), .pin9(Adder_Cout));
  _7432 u_7432_1 (
    .pin1(A[5]), .pin2(B[5]), .pin3(or5), .pin4(A[4]), .pin5(B[4]), .pin6(or4), .pin13(A[6]), .pin12(B[6]),
    .pin11(or6), .pin10(A[7]), .pin9(B[7]), .pin8(or7));
  _7402 u_7402_1 (
    .pin1(n7402_1_pin1), .pin2(Result[0]), .pin3(Result[1]), .pin4(n7402_1_pin4), .pin5(Result[2]),
    .pin6(Result[3]), .pin13(n7402_1_pin13), .pin12(NF_out), .pin11(Result[6]), .pin10(n7402_1_pin10),
    .pin9(Result[5]), .pin8(Result[4]));
  _7408 u_7408_3 (
    .pin1(n7402_1_pin13), .pin2(n7402_1_pin10), .pin3(n7408_3_pin3), .pin13(n7402_1_pin1),
    .pin12(n7402_1_pin4), .pin11(n7408_3_pin11), .pin10(n7408_3_pin11), .pin9(n7408_3_pin3), .pin8(ZF_out));  // open: pin4, pin5, pin6
  _74283 u_74283_2 (
    .pin1(add1), .pin2(Bx1), .pin3(A[1]), .pin4(add0), .pin5(A[0]), .pin6(Bx0), .pin7(Cin), .pin15(Bx2),
    .pin14(A[2]), .pin13(add2), .pin12(A[3]), .pin11(Bx3), .pin10(add3), .pin9(n74283_1_pin7));
  _7432 u_7432_2 (
    .pin1(A[1]), .pin2(B[1]), .pin3(or1), .pin4(A[0]), .pin5(B[0]), .pin6(or0), .pin13(A[2]), .pin12(B[2]),
    .pin11(or2), .pin10(A[3]), .pin9(B[3]), .pin8(or3));
  _7400 u_7400_1 (
    .pin4(Sel_adder), .pin5(Adder_Cout), .pin6(n7400_1_pin6), .pin13(SHR), .pin12(A[0]),
    .pin11(n7400_1_pin11), .pin10(n7400_1_pin11), .pin9(n7400_1_pin6), .pin8(CF_out));  // open: pin1, pin2, pin3
  _74157 u_74157_1 (
    .pin1(Sel_adder), .pin2(mux5), .pin3(add5), .pin4(Result[5]), .pin5(mux4), .pin6(add4), .pin7(Result[4]),
    .pin15(n74157_1_pin15), .pin14(mux6), .pin13(add6), .pin12(Result[6]), .pin11(mux7), .pin10(add7),
    .pin9(NF_out));
  _74153 u_74153_1 (
    .pin1(n74153_1_pin1), .pin2(S1), .pin3(A[6]), .pin4(xor5), .pin5(or5), .pin6(and5), .pin7(mux5),
    .pin15(n74153_1_pin15), .pin14(S0), .pin13(A[7]), .pin12(xor6), .pin11(or6), .pin10(and6), .pin9(mux6));
  _74153 #(.ShowInternalStructure("true")) u_74153_2 (
    .pin1(n74153_2_pin1), .pin2(S1), .pin3(A[2]), .pin4(xor1), .pin5(or1), .pin6(and1), .pin7(mux1),
    .pin15(n74153_2_pin15), .pin14(S0), .pin13(A[3]), .pin12(xor2), .pin11(or2), .pin10(and2), .pin9(mux2));
  _74157 u_74157_2 (
    .pin1(Sel_adder), .pin2(mux1), .pin3(add1), .pin4(Result[1]), .pin5(mux0), .pin6(add0), .pin7(Result[0]),
    .pin15(n74157_2_pin15), .pin14(mux2), .pin13(add2), .pin12(Result[2]), .pin11(mux3), .pin10(add3),
    .pin9(Result[3]));
  _74153 u_74153_3 (
    .pin1(n74153_3_pin1), .pin2(S1), .pin3(A[5]), .pin4(xor4), .pin5(or4), .pin6(and4), .pin7(mux4),
    .pin15(n74153_3_pin15), .pin14(S0), .pin13(shr7), .pin12(xor7), .pin11(or7), .pin10(and7), .pin9(mux7));
  _74153 u_74153_4 (
    .pin1(n74153_4_pin1), .pin2(S1), .pin3(A[1]), .pin4(xor0), .pin5(or0), .pin6(and0), .pin7(mux0),
    .pin15(n74153_4_pin15), .pin14(S0), .pin13(A[4]), .pin12(xor3), .pin11(or3), .pin10(and3), .pin9(mux3));

  assign Result[7] = NF_out;
  // also tied to GND on the sheet: {n74153_1_pin1, n74153_2_pin1, n74157_1_pin15, n74153_1_pin15, n74153_2_pin15, n74153_3_pin1, n74153_4_pin1, n74157_2_pin15, n74153_3_pin15, n74153_4_pin15, shr7}

  // Other names for the same wires on the sheet: ALU_A[7:0] = A; SHR_Cout = A[0]; shr0 = A[1]; shr1 = A[2];
  //   shr2 = A[3]; shr3 = A[4]; shr4 = A[5]; shr5 = A[6]; shr6 = A[7]; ALU_B[7:0] = B; ALU_CF = CF_out;
  //   ALU_out[7:0] = {NF_out, Result[6:0]}; out0 = Result[0]; out1 = Result[1]; out2 = Result[2]; out3 = Result[3];
  //   out4 = Result[4]; out5 = Result[5]; out6 = Result[6]; ALU_NF = NF_out; out7 = NF_out; ALU_ZF = ZF_out;
  //   Sel_s0 = S0; Sel_s1 = S1
endmodule

module Register_Module (
  input  [7:0] Data_in,
  input  n_Write_en,
  input  CLK,
  input  Reset,
  output [7:0] Reg_out
);

  TTL_74173 ttl_74173_1 (
    .M(1'b0), .N(1'b0), .nG2(1'b0), .nG1(n_Write_en), .CLK(CLK), .D1(Data_in[7]), .D2(Data_in[6]),
    .D3(Data_in[5]), .D4(Data_in[4]), .CLR(Reset), .Q1(Reg_out[7]), .Q2(Reg_out[6]), .Q3(Reg_out[5]),
    .Q4(Reg_out[4]));
  TTL_74173 ttl_74173_2 (
    .M(1'b0), .N(1'b0), .nG2(1'b0), .nG1(n_Write_en), .CLK(CLK), .D1(Data_in[3]), .D2(Data_in[2]),
    .D3(Data_in[1]), .D4(Data_in[0]), .CLR(Reset), .Q1(Reg_out[3]), .Q2(Reg_out[2]), .Q3(Reg_out[1]),
    .Q4(Reg_out[0]));
  LED led_1 (.in(Reg_out[7]));
  LED led_2 (.in(Reg_out[6]));
  LED led_3 (.in(Reg_out[5]));
  LED led_4 (.in(Reg_out[4]));
  LED led_5 (.in(Reg_out[3]));
  LED led_6 (.in(Reg_out[2]));
  LED led_7 (.in(Reg_out[1]));
  LED led_8 (.in(Reg_out[0]));
endmodule

module Tri_state_Module (
  input  [7:0] Data_in,
  input  n_Enable,
  output [7:0] Data_out
);

  wire n74541_1_pin19;

  _74541 u_74541_1 (
    .pin1(n_Enable), .pin2(Data_in[0]), .pin3(Data_in[1]), .pin4(Data_in[2]), .pin5(Data_in[3]),
    .pin6(Data_in[4]), .pin7(Data_in[5]), .pin8(Data_in[6]), .pin9(Data_in[7]), .pin19(n74541_1_pin19),
    .pin18(Data_out[0]), .pin17(Data_out[1]), .pin16(Data_out[2]), .pin15(Data_out[3]), .pin14(Data_out[4]),
    .pin13(Data_out[5]), .pin12(Data_out[6]), .pin11(Data_out[7]));
  // also tied to GND on the sheet: n74541_1_pin19
endmodule

module PC_Module (
  input  [7:0] Jump_addr,
  input  CLK,
  input  Count_en,
  input  n_Reset,
  input  n_Jump_en,
  output [7:0] PC_out
);

  wire n74161_1_pin10, n74161_2_pin10;

  _74161 u_74161_1 (
    .pin1(n_Reset), .pin2(CLK), .pin3(Jump_addr[4]), .pin4(Jump_addr[5]), .pin5(Jump_addr[6]),
    .pin6(Jump_addr[7]), .pin7(Count_en), .pin14(PC_out[4]), .pin13(PC_out[5]), .pin12(PC_out[6]),
    .pin11(PC_out[7]), .pin10(n74161_1_pin10), .pin9(n_Jump_en));  // open: pin15
  _74161 u_74161_2 (
    .pin1(n_Reset), .pin2(CLK), .pin3(Jump_addr[0]), .pin4(Jump_addr[1]), .pin5(Jump_addr[2]),
    .pin6(Jump_addr[3]), .pin7(Count_en), .pin15(n74161_1_pin10), .pin14(PC_out[0]), .pin13(PC_out[1]),
    .pin12(PC_out[2]), .pin11(PC_out[3]), .pin10(n74161_2_pin10), .pin9(n_Jump_en));
  LED led_1 (.in(PC_out[7]));
  LED led_2 (.in(PC_out[6]));
  LED led_3 (.in(PC_out[5]));
  LED led_4 (.in(PC_out[4]));
  LED led_5 (.in(PC_out[3]));
  LED led_6 (.in(PC_out[0]));
  LED led_7 (.in(PC_out[2]));
  LED led_8 (.in(PC_out[1]));
  // also tied to VCC on the sheet: n74161_2_pin10
endmodule

module Status_Flags_Module (
  input  ZF_in,
  input  NF_in,
  input  CF_in,
  input  n_ALU_en,
  input  n_Set_CF,
  input  CLK,
  input  Reset,
  output ZF_out,
  output NF_out,
  output CF_out
);

  wire n7400_1_pin3, n7400_1_pin5, n7400_1_pin6, n7400_1_pin11, n7400_2_pin3, n7400_2_pin5, n7400_2_pin6,
       n7400_2_pin11, n7400_3_pin3, n7400_3_pin5, n7400_3_pin6, n7400_3_pin11;

  _7400 #(.ShowInternalStructure("true")) u_7400_1 (
    .pin1(ZF_out), .pin2(n_ALU_en), .pin3(n7400_1_pin3), .pin4(n7400_1_pin3), .pin5(n7400_1_pin5),
    .pin6(n7400_1_pin6), .pin13(n_ALU_en), .pin12(n_ALU_en), .pin11(n7400_1_pin11), .pin10(n7400_1_pin11),
    .pin9(ZF_in), .pin8(n7400_1_pin5));
  _7400 #(.ShowInternalStructure("true")) u_7400_2 (
    .pin1(NF_out), .pin2(n_ALU_en), .pin3(n7400_2_pin3), .pin4(n7400_2_pin3), .pin5(n7400_2_pin5),
    .pin6(n7400_2_pin6), .pin13(n_ALU_en), .pin12(n_ALU_en), .pin11(n7400_2_pin11), .pin10(n7400_2_pin11),
    .pin9(NF_in), .pin8(n7400_2_pin5));
  _7400 #(.ShowInternalStructure("true")) u_7400_3 (
    .pin1(CF_out), .pin2(n_Set_CF), .pin3(n7400_3_pin3), .pin4(n7400_3_pin3), .pin5(n7400_3_pin5),
    .pin6(n7400_3_pin6), .pin13(n_Set_CF), .pin12(n_Set_CF), .pin11(n7400_3_pin11), .pin10(n7400_3_pin11),
    .pin9(CF_in), .pin8(n7400_3_pin5));
  TTL_74173 ttl_74173_1 (
    .M(1'b0), .N(1'b0), .nG2(1'b0), .nG1(1'b0), .CLK(CLK), .D1(n7400_1_pin6), .D2(n7400_2_pin6),
    .D3(n7400_3_pin6), .CLR(Reset), .Q1(ZF_out), .Q2(NF_out), .Q3(CF_out));  // open: D4, Q4

  // Other names for the same wires on the sheet: ALU_sel = n_ALU_en; CF_curr = CF_out; CF_sel = n_Set_CF;
  //   NF_curr = NF_out; ZF_curr = ZF_out
endmodule

module Mux_2_to_1_8_bit_Module (
  input  [7:0] A,
  input  [7:0] B,
  input  Sel,
  output [7:0] Y
);

  wire n74157_1_pin15;

  _74157 u_74157_1 (
    .pin1(Sel), .pin2(A[7]), .pin3(B[7]), .pin4(Y[7]), .pin5(A[6]), .pin6(B[6]), .pin7(Y[6]),
    .pin15(n74157_1_pin15), .pin14(A[5]), .pin13(B[5]), .pin12(Y[5]), .pin11(A[4]), .pin10(B[4]), .pin9(Y[4]));
  _74157 u_74157_2 (
    .pin1(Sel), .pin2(A[3]), .pin3(B[3]), .pin4(Y[3]), .pin5(A[2]), .pin6(B[2]), .pin7(Y[2]),
    .pin15(n74157_1_pin15), .pin14(A[1]), .pin13(B[1]), .pin12(Y[1]), .pin11(A[0]), .pin10(B[0]), .pin9(Y[0]));
  // also tied to GND on the sheet: n74157_1_pin15
endmodule

module Error_detector (
  input  in_1,
  output out_2
);

  wire pull_resistor_1_node, register_1_q;

  Pull_Resistor pull_resistor_1 (.node(pull_resistor_1_node));
  BitSelector #(.width(2)) bitselector_1 (.in(2'b11), .out(pull_resistor_1_node), .sel(out_2));
  Register #(.trigger("low"), .width(1)) register_1 (
    .D(in_1), .en(pull_resistor_1_node), .clk(1'b0), .Q(register_1_q));  // open: clr
  xnor xnor_1 (out_2, register_1_q, register_1_q);
endmodule
