// Logisim project PFC_mini.circ as structural Verilog: 5 circuits, main circuit main
module main (
  input  Start,
  input  Reset,
  input  in_3,
  input  in_4
);

  wire ADDR_A, ADDR_B, ADDR_C, ADDR_D, ADDR_Opnd, ALU_CF, ALU_En, ALU_NF, ALU_OF, ALU_ZF, and_1_out,
       and_2_out, and_3_out, and_4_out, and_5_out, and_6_out, and_8_out, and_9_out, and_10_out, and_11_out,
       and_12_out, and_13_out, and_14_out, clock_1_out, clock_2_out, clock_4_out, clock_6_out, clock_7_out,
       clock_8_out, clock_9_out, clock_10_out, clock_11_out, clock_12_out, clock_13_out, clock_14_out,
       clock_15_out, clock_16_out, clock_17_out, clock_18_out, decoder_1_out6, decoder_1_out7, Execute_1,
       Execute_2, Fetch_1, Fetch_2, Idle, In_0_En, In_1_En, In_2_En, In_3_En, Jump_En, MMIO,
       multiplexer_2_out, multiplexer_3_out, multiplexer_4_out, multiplexer_6_out, multiplexer_7_out,
       not_1_out, or_1_out, random_1_p2, Reset_t, S_CF, S_NF, S_OF, S_ZF, Set_PC, Start_t, xor_1_out;
  wire [2:0] CPU_state;
  wire [3:0] bin_to_bcd_16_1_out_1, bin_to_bcd_16_1_out_10, bin_to_bcd_16_1_out_100,
       bin_to_bcd_16_1_out_1000, bin_to_bcd_16_1_out_10000, Buttons, In_0;
  wire [7:0] A, Address, Address_bus, ALU_out, B, C, D, Data_bus, In_1, In_2, In_3_t,
       led_matrix_driver_1_row_0, led_matrix_driver_1_row_1, led_matrix_driver_1_row_2,
       led_matrix_driver_1_row_3, led_matrix_driver_1_row_4, led_matrix_driver_1_row_5,
       led_matrix_driver_1_row_6, led_matrix_driver_1_row_7, multiplexer_1_out, multiplexer_5_out, Opcode,
       Operand, PC, PC_plus_1, Program_out, register_1_q;
  wire [15:0] register_2_q;
  wire [21:0] Control_signals;

  and and_1 (and_1_out, In_1_En, Control_signals[4]);
  Register register_1 (.D(Data_bus), .en(and_2_out), .clk(clock_1_out), .Q(register_1_q));  // open: clr
  and and_2 (and_2_out, Control_signals[4], In_0_En);
  Clock clock_1 (.out(clock_1_out));
  and and_3 (and_3_out, Control_signals[4], In_1_En);
  Hex_Digit_Display hex_digit_display_1 (.value(A[7:4]));  // open: dp
  Hex_Digit_Display hex_digit_display_2 (.value(A[3:0]));  // open: dp
  Hex_Digit_Display hex_digit_display_3 (.value(C[7:4]));  // open: dp
  Hex_Digit_Display hex_digit_display_4 (.value(C[3:0]));  // open: dp
  Hex_Digit_Display hex_digit_display_5 (.value(PC[7:4]));  // open: dp
  Hex_Digit_Display hex_digit_display_6 (.value(PC[3:0]));  // open: dp
  LED_Matrix_Driver led_matrix_driver_1 (
    .Data(Data_bus), .Data_en(and_4_out), .Start_data(and_5_out), .Stop_data(and_6_out), .Reset(Reset_t),
    .Row_7(led_matrix_driver_1_row_7), .Row_0(led_matrix_driver_1_row_0), .Row_1(led_matrix_driver_1_row_1),
    .Row_2(led_matrix_driver_1_row_2), .Row_3(led_matrix_driver_1_row_3), .Row_4(led_matrix_driver_1_row_4),
    .Row_5(led_matrix_driver_1_row_5), .Row_6(led_matrix_driver_1_row_6));
  and and_4 (and_4_out, In_0_En, Control_signals[4]);
  and and_5 (and_5_out, Data_bus[0], and_1_out);
  and and_6 (and_6_out, Data_bus[1], and_1_out);
  or or_1 (or_1_out, Buttons[0], Buttons[1], Buttons[2], Buttons[3]);
  Register #(.width(16)) register_2 (
    .D({Data_bus, register_1_q}), .en(and_3_out), .clk(clock_2_out), .Q(register_2_q));  // open: clr
  Clock clock_2 (.out(clock_2_out));
  Clock clock_3 ();  // open: out
  DotMatrix #(.dotshape("circle"), .inputtype("row"), .matrixcols(8), .matrixrows(8), .persist(300)) dotmatrix_1 (
    .row0(led_matrix_driver_1_row_0), .row1(led_matrix_driver_1_row_1), .row2(led_matrix_driver_1_row_2),
    .row3(led_matrix_driver_1_row_3), .row4(led_matrix_driver_1_row_4), .row5(led_matrix_driver_1_row_5),
    .row6(led_matrix_driver_1_row_6), .row7(led_matrix_driver_1_row_7));
  Button button_1 (.out(Buttons[0]));
  Button button_2 (.out(Buttons[3]));
  Button button_3 (.out(Buttons[1]));
  Register #(.width(4)) register_3 (.D(Buttons), .en(or_1_out), .clk(clock_4_out), .Q(In_0), .clr(Reset_t));
  Clock clock_4 (.out(clock_4_out));
  Hex_Digit_Display hex_digit_display_7 (.value(bin_to_bcd_16_1_out_10000));  // open: dp
  Hex_Digit_Display hex_digit_display_8 (.value(bin_to_bcd_16_1_out_1000));  // open: dp
  or or_2 (Start_t, Start, in_3);
  or or_3 (Reset_t, Reset, in_4);
  Hex_Digit_Display hex_digit_display_9 (.value(B[7:4]));  // open: dp
  Hex_Digit_Display hex_digit_display_10 (.value(B[3:0]));  // open: dp
  Hex_Digit_Display hex_digit_display_11 (.value(D[7:4]));  // open: dp
  Hex_Digit_Display hex_digit_display_12 (.value(D[3:0]));  // open: dp
  LED led_1 (.in(Idle));
  LED led_2 (.in(Fetch_1));
  LED led_3 (.in(Fetch_2));
  LED led_4 (.in(Execute_1));
  LED led_5 (.in(Execute_2));
  Button button_4 (.out(Buttons[2]));
  // Random random_1: pin names not known; wires that end beside it: 1'b1, random_1_p2
  Clock clock_5 (.out(random_1_p2));
  Hex_Digit_Display hex_digit_display_13 (.value(bin_to_bcd_16_1_out_100));  // open: dp
  Hex_Digit_Display hex_digit_display_14 (.value(bin_to_bcd_16_1_out_10));  // open: dp
  Bin_to_BCD_16 bin_to_bcd_16_1 (
    .Bin(register_2_q), .Out_1(bin_to_bcd_16_1_out_1), .Out_10(bin_to_bcd_16_1_out_10),
    .Out_100(bin_to_bcd_16_1_out_100), .Out_1000(bin_to_bcd_16_1_out_1000),
    .Out_10000(bin_to_bcd_16_1_out_10000));
  Hex_Digit_Display hex_digit_display_15 (.value(bin_to_bcd_16_1_out_1));  // open: dp
  Multiplexer #(.width(8)) multiplexer_1 (.in0(Data_bus), .in1(ALU_out), .out(multiplexer_1_out), .sel(ALU_En));
  Register u_A (.D(multiplexer_1_out), .en(Control_signals[0]), .clk(clock_6_out), .Q(A), .clr(Reset_t));
  Clock clock_6 (.out(clock_6_out));
  D_Flip_Flop Flag_ZF (.D(multiplexer_2_out), .clk(clock_7_out), .Q(S_ZF), .reset(Reset_t));  // open: Qn, preset
  Multiplexer multiplexer_2 (.in0(S_ZF), .in1(ALU_ZF), .out(multiplexer_2_out), .sel(ALU_En));
  Clock clock_7 (.out(clock_7_out));
  ROM Program_Memory (.addr(PC), .data(Program_out));
  and and_7 (MMIO, Address[2], Address[3], Address[4], Address[5], Address[6], Address[7]);
  Register MAR (.D(Address_bus), .en(Execute_1), .clk(clock_8_out), .Q(Address), .clr(Reset_t));
  Clock clock_8 (.out(clock_8_out));
  Control_Unit control_unit_1 (
    .Start(Start_t), .Program_out(Program_out), .Opcode(Opcode), .Reset(Reset_t), .CPU_state(CPU_state),
    .Control_signals({Control_signals[21:17], ALU_En, ADDR_Opnd, ADDR_D, ADDR_C, ADDR_B, ADDR_A, Control_signals[10:0]}));
  Clock clock_9 (.out(clock_9_out));
  Register u_B (.D(Data_bus), .en(Control_signals[1]), .clk(clock_10_out), .Q(B), .clr(Reset_t));
  Clock clock_10 (.out(clock_10_out));
  D_Flip_Flop Flag_NF (.D(multiplexer_3_out), .clk(clock_9_out), .Q(S_NF), .reset(Reset_t));  // open: Qn, preset
  Multiplexer multiplexer_3 (.in0(S_NF), .in1(ALU_NF), .out(multiplexer_3_out), .sel(ALU_En));
  Clock clock_11 (.out(clock_11_out));
  Decoder #(.enable("false"), .select(3)) decoder_1 (
    .out0(Idle), .out1(Fetch_1), .out4(Execute_2), .out5(Execute_1), .out6(decoder_1_out6),
    .out7(decoder_1_out7), .sel(CPU_state));  // open: out2, out3
  RAM #(.databus("bidir"), .enables("line"), .trigger("high")) Data_Memory (
    .addr(Address), .we(and_8_out), .oe(and_9_out), .clk(not_1_out), .data(Data_bus));
  and and_8 (and_8_out, Control_signals[4], not_1_out, clock_11_out);
  and and_9 (and_9_out, Control_signals[9], not_1_out);
  not not_1 (not_1_out, MMIO);
  or or_4 (Fetch_2, decoder_1_out6, decoder_1_out7);
  Register u_C (.D(Data_bus), .en(Control_signals[2]), .clk(clock_12_out), .Q(C), .clr(Reset_t));
  Clock clock_12 (.out(clock_12_out));
  D_Flip_Flop Flag_CF (.D(multiplexer_4_out), .clk(clock_13_out), .Q(S_CF), .reset(Reset_t));  // open: Qn, preset
  Multiplexer multiplexer_4 (.in0(S_CF), .in1(ALU_CF), .out(multiplexer_4_out), .sel(Control_signals[17]));
  Clock clock_13 (.out(clock_13_out));
  Multiplexer #(.width(8)) multiplexer_5 (.in0(PC_plus_1), .in1(Operand), .out(multiplexer_5_out), .sel(Jump_En));
  or or_5 (Set_PC, Fetch_1, Fetch_2, Jump_En);
  Multiplexer #(.select(2)) multiplexer_6 (
    .in0(S_ZF), .in1(S_NF), .in2(S_CF), .in3(S_OF), .out(multiplexer_6_out), .sel(Opcode[1:0]));
  xor xor_1 (xor_1_out, multiplexer_6_out, Opcode[2]);
  Register u_D (.D(Data_bus), .en(Control_signals[3]), .clk(clock_14_out), .Q(D), .clr(Reset_t));
  Clock clock_14 (.out(clock_14_out));
  D_Flip_Flop Flag_OF (.D(multiplexer_7_out), .clk(clock_15_out), .Q(S_OF), .reset(Reset_t));  // open: Qn, preset
  Multiplexer multiplexer_7 (.in0(S_OF), .in1(ALU_OF), .out(multiplexer_7_out), .sel(Control_signals[18]));
  Clock clock_15 (.out(clock_15_out));
  Register u_PC (.D(multiplexer_5_out), .en(Set_PC), .clk(clock_16_out), .Q(PC), .clr(Reset_t));
  Clock clock_16 (.out(clock_16_out));
  and and_10 (and_10_out, Control_signals[20], xor_1_out);
  Adder adder_1 (.a(PC), .b(8'h1), .out(PC_plus_1), .cin(1'b0));  // open: cout
  or or_6 (Jump_En, Control_signals[19], and_10_out);
  Decoder #(.select(2)) decoder_2 (
    .out0(In_0_En), .out1(In_1_En), .out2(In_2_En), .out3(In_3_En), .sel(Address[1:0]), .en(MMIO));
  assign Data_bus = Control_signals[5] ? A : 8'bz;  // Controlled_Buffer controlled_buffer_1
  assign Data_bus = Control_signals[6] ? B : 8'bz;  // Controlled_Buffer controlled_buffer_2
  assign Data_bus = Control_signals[7] ? C : 8'bz;  // Controlled_Buffer controlled_buffer_3
  assign Data_bus = Control_signals[8] ? D : 8'bz;  // Controlled_Buffer controlled_buffer_4
  assign Data_bus = Control_signals[10] ? Operand : 8'bz;  // Controlled_Buffer controlled_buffer_5
  Pull_Resistor pull_resistor_1 (.node(Data_bus));
  Register u_Opcode (.D(Program_out), .en(Fetch_1), .clk(clock_17_out), .Q(Opcode), .clr(Reset_t));
  Clock clock_17 (.out(clock_17_out));
  Register u_Operand (.D(Program_out), .en(Fetch_2), .clk(clock_18_out), .Q(Operand), .clr(Reset_t));
  Clock clock_18 (.out(clock_18_out));
  and and_11 (and_11_out, Control_signals[9], In_0_En);
  and and_12 (and_12_out, Control_signals[9], In_1_En);
  and and_13 (and_13_out, Control_signals[9], In_2_En);
  and and_14 (and_14_out, Control_signals[9], In_3_En);
  assign Data_bus = and_11_out ? {4'b0000, In_0} : 8'bz;  // Controlled_Buffer controlled_buffer_6
  assign Data_bus = and_12_out ? In_1 : 8'bz;  // Controlled_Buffer controlled_buffer_7
  assign Data_bus = and_13_out ? In_2 : 8'bz;  // Controlled_Buffer controlled_buffer_8
  assign Data_bus = and_14_out ? In_3_t : 8'bz;  // Controlled_Buffer controlled_buffer_9
  assign Address_bus = ADDR_A ? A : 8'bz;  // Controlled_Buffer controlled_buffer_10
  assign Address_bus = ADDR_B ? B : 8'bz;  // Controlled_Buffer controlled_buffer_11
  assign Address_bus = ADDR_C ? C : 8'bz;  // Controlled_Buffer controlled_buffer_12
  assign Address_bus = ADDR_D ? D : 8'bz;  // Controlled_Buffer controlled_buffer_13
  assign Address_bus = ADDR_Opnd ? Operand : 8'bz;  // Controlled_Buffer controlled_buffer_14
  ALU alu_1 (
    .Opcode(Opcode), .A(A), .B(Data_bus), .CF_in(S_CF), .Result(ALU_out), .ZF_out(ALU_ZF), .NF_out(ALU_NF),
    .CF_out(ALU_CF), .OF_out(ALU_OF));
  Pull_Resistor pull_resistor_2 (.node(Address_bus));

  // Other names for the same wires on the sheet: WR_A = Control_signals[0]; WR_B = Control_signals[1];
  //   WR_C = Control_signals[2]; WR_D = Control_signals[3]; WR_RAM = Control_signals[4]; RD_A = Control_signals[5];
  //   RD_B = Control_signals[6]; RD_C = Control_signals[7]; RD_D = Control_signals[8]; RD_RAM = Control_signals[9];
  //   RD_Opnd = Control_signals[10]; Control_signals[16:11] = {ALU_En, ADDR_Opnd, ADDR_D, ADDR_C, ADDR_B, ADDR_A};
  //   Set_CF = Control_signals[17]; Set_OF = Control_signals[18]; JMP = Control_signals[19];
  //   JMP_Cond = Control_signals[20]; Halt = Control_signals[21]; Reset_2 = in_4; Start_2 = in_3

  // Notes on the sheet:
  //   contents of Program_Memory (hex, n*v repeats v):
  //   10 8 14 1 18 0 94 1 39 15 44 c 90 20 48 1 80 4 3 30 6 10 4 50 10 10 40 50 11 10 1b 50 13 70 fd b0 3f
  //   50 12 30 89 70 fc d4 0 38 31 50 10 74 40 1 b0 38 ac ac ac 90 20 c 1 b0 7 60 b8 ff 67 a1 43 70 11 68
  //   74 10 1 b0 1 38 54 2 94 8 30 73 1 b0 2 38 5e 2 90 8 30 73 1 b0 4 38 68 2 90 1 30 6b 2 94 1 b0 7 4 2
  //   b0 38 30 79 b0 38 4 2 b0 7 a5 50 13 74 12 c5 3c 89 70 11 90 1 50 11 30 21 10 40 18 1 82 64 86 44 82
  //   4 94 7f 1 3c 8d 70 13 74 11 41 4 b0 38 ac ac ac 90 20 c 1 b0 7 64 63 a5 43 74 12 1 b0 38 ac ac ac 90
  //   20 c 1 b0 7 64 63 a5 43 10 1 50 fd 10 20 64 54 fc 90 1 d4 28 3c c5 10 2 50 fd 30 29 28
endmodule

module Control_Unit (
  input  Start,
  input  [7:0] Program_out,
  input  [7:0] Opcode,
  input  Reset,
  output [2:0] CPU_state,
  output [21:0] Control_signals
);

  wire ALU_En_ROM, clock_1_out, decoder_1_out6, decoder_1_out7, Execute_1, Execute_2, Fetch_1, Fetch_2, Idle,
       Length_2, Set_CF_ROM, Set_OF_ROM, WR_MAR;
  wire [1:0] Control;
  wire [2:0] ADDR, CPU_next_state, RD, WR;
  wire [3:2] undriven, undriven_2;
  wire [4:2] undriven_3;
  wire [7:0] multiplexer_4_out;

  not not_1 (undriven_3[4], Control_signals[21]);
  Register #(.width(3)) CPU_state_reg (.D(CPU_next_state), .en(1'b1), .clk(clock_1_out), .Q(CPU_state), .clr(Reset));
  Clock clock_1 (.out(clock_1_out));
  Multiplexer #(.select(3)) multiplexer_1 (
    .in0(1'b0), .in1(1'b1), .in2(undriven[2]), .in3(undriven[3]), .in4(1'b0), .in5(1'b1), .in6(1'b1),
    .in7(1'b1), .out(CPU_next_state[2]), .sel(CPU_state));
  Multiplexer #(.select(3)) multiplexer_2 (
    .in0(1'b0), .in1(Length_2), .in2(undriven_2[2]), .in3(undriven_2[3]), .in4(1'b0), .in5(1'b0), .in6(1'b0),
    .in7(1'b0), .out(CPU_next_state[1]), .sel(CPU_state));
  Multiplexer #(.select(3)) multiplexer_3 (
    .in0(Start), .in1(WR_MAR), .in2(undriven_3[2]), .in3(undriven_3[3]), .in4(undriven_3[4]), .in5(1'b0),
    .in6(WR_MAR), .in7(WR_MAR), .out(CPU_next_state[0]), .sel(CPU_state));
  Decoder #(.enable("false"), .select(3)) decoder_1 (
    .out0(Idle), .out1(Fetch_1), .out4(Execute_2), .out5(Execute_1), .out6(decoder_1_out6),
    .out7(decoder_1_out7), .sel(CPU_state));  // open: out2, out3
  Multiplexer #(.width(8)) multiplexer_4 (.in0(Opcode), .in1(Program_out), .out(multiplexer_4_out), .sel(Fetch_1));
  Decoder #(.select(3)) decoder_2 (
    .out1(Control_signals[4]), .out4(Control_signals[0]), .out5(Control_signals[1]),
    .out6(Control_signals[2]), .out7(Control_signals[3]), .sel(WR), .en(Execute_2));  // open: out0, out2, out3
  Decoder #(.select(3)) decoder_3 (
    .out1(Control_signals[9]), .out2(Control_signals[10]), .out4(Control_signals[5]),
    .out5(Control_signals[6]), .out6(Control_signals[7]), .out7(Control_signals[8]), .sel(RD), .en(Execute_2));  // open: out0, out3
  Decoder #(.select(3)) decoder_4 (
    .out1(Control_signals[15]), .out4(Control_signals[11]), .out5(Control_signals[12]),
    .out6(Control_signals[13]), .out7(Control_signals[14]), .sel(ADDR), .en(Execute_1));  // open: out0, out2, out3
  Decoder #(.select(2)) decoder_5 (
    .out1(Control_signals[19]), .out2(Control_signals[20]), .out3(Control_signals[21]), .sel(Control),
    .en(Execute_2));  // open: out0
  or or_1 (Fetch_2, decoder_1_out6, decoder_1_out7);
  ROM uCode_ROM_1 (.addr(multiplexer_4_out), .data({RD, WR, WR_MAR, Length_2}));
  ROM uCode_ROM_2 (.addr(multiplexer_4_out), .data({Control, Set_OF_ROM, Set_CF_ROM, ALU_En_ROM, ADDR}));
  and and_1 (Control_signals[16], ALU_En_ROM, Execute_2);
  and and_2 (Control_signals[17], Set_CF_ROM, Execute_2);
  and and_3 (Control_signals[18], Set_OF_ROM, Execute_2);

  // Other names for the same wires on the sheet: WR_A = Control_signals[0]; WR_B = Control_signals[1];
  //   WR_C = Control_signals[2]; WR_D = Control_signals[3]; WR_RAM = Control_signals[4]; RD_A = Control_signals[5];
  //   RD_B = Control_signals[6]; RD_C = Control_signals[7]; RD_D = Control_signals[8]; RD_RAM = Control_signals[9];
  //   RD_Opnd = Control_signals[10]; ADDR_A = Control_signals[11]; ADDR_B = Control_signals[12];
  //   ADDR_C = Control_signals[13]; ADDR_D = Control_signals[14]; ADDR_Opnd = Control_signals[15];
  //   ALU_En = Control_signals[16]; Set_CF = Control_signals[17]; Set_OF = Control_signals[18];
  //   JMP = Control_signals[19]; JMP_Cond = Control_signals[20]; Halt = Control_signals[21]

  // Notes on the sheet:
  //   contents of uCode_ROM_1 (hex, n*v repeats v):
  //   90 b0 d0 f0 94 b4 d4 f4 98 b8 d8 f8 9c bc dc fc 4*51 4*55 4*59 4*5d 16*0 16*1 4*86 4*a6 4*c6 4*e6
  //   4*87 4*a7 4*c7 4*e7 4*32 4*36 4*3a 4*3e 4*33 4*37 4*3b 4*3f 90 b0 d0 f0 90 b0 d0 f0 90 b0 d0 f0 90
  //   b0 d0 f0 16*51 90 b0 d0 f0 90 b0 d0 f0 90 b0 d0 f0 4*10 12*51 4*10 4*0 80 a0 c0 e0 12*0 4*41 8*0 80
  //   a0 c0 e0 12*0 4*41
  //   contents of uCode_ROM_2 (hex, n*v repeats v):
  //   40*0 8*c0 8*40 8*80 4 5 6 7 4 5 6 7 4 5 6 7 4 5 6 7 16*1 4 5 6 7 4 5 6 7 4 5 6 7 4 5 6 7 16*1 32*38
  //   12*8 4*18 12*8 4*18 4*0 4*38 12*0 4*38 8*0 4*8 12*0 4*8
endmodule

module ALU (
  input  [7:0] Opcode,
  input  [7:0] A,
  input  [7:0] B,
  input  CF_in,
  output [7:0] Result,
  output ZF_out,
  output NF_out,
  output CF_out,
  output OF_out
);

  wire Adder_Cin, Adder_Cout, ALU_ADC, ALU_ADD, ALU_AND, ALU_OR, ALU_ROR, ALU_SBC, ALU_SHR, ALU_SHR_ROR,
       ALU_SUB, ALU_subtract, ALU_XOR, and_1_out, and_6_out, and_7_out, and_8_out, and_9_out, and_10_out,
       and_11_out, not_1_out, not_2_out, not_3_out, not_4_out, not_5_out, not_6_out, or_1_out, ROR_Cin;
  wire [7:0] adder_1_out, and_5_out, bit_extender_1_out, multiplexer_1_out, or_4_out, xor_1_out, xor_2_out;

  or or_1 (or_1_out, ALU_ADC, ALU_SBC);
  Decoder #(.enable("false"), .select(3)) decoder_1 (
    .out0(ALU_ADD), .out1(ALU_SUB), .out2(ALU_ADC), .out3(ALU_SBC), .out4(ALU_AND), .out5(ALU_OR),
    .out6(ALU_XOR), .out7(ALU_SHR_ROR), .sel({Opcode[5], Opcode[3:2]}));
  or or_2 (ALU_subtract, ALU_SUB, ALU_SBC);
  or or_3 (Adder_Cin, ALU_SUB, and_1_out);
  and and_1 (and_1_out, or_1_out, CF_in);
  and and_2 (ALU_SHR, ALU_SHR_ROR, not_1_out);
  not not_1 (not_1_out, Opcode[5]);
  and and_3 (ALU_ROR, ALU_SHR_ROR, Opcode[5]);
  and and_4 (ROR_Cin, CF_in, ALU_ROR);
  assign bit_extender_1_out = {{7{ALU_subtract}}, ALU_subtract};  // Bit_Extender bit_extender_1
  assign xor_1_out = B ^ bit_extender_1_out;  // XOR_Gate xor_1, 8 bits wide
  assign and_5_out = A & B;  // AND_Gate and_5, 8 bits wide
  assign or_4_out = A | B;  // OR_Gate or_4, 8 bits wide
  assign xor_2_out = A ^ B;  // XOR_Gate xor_2, 8 bits wide
  Adder adder_1 (.a(A), .b(xor_1_out), .out(adder_1_out), .cin(Adder_Cin), .cout(Adder_Cout));
  Multiplexer #(.select(2), .width(8)) multiplexer_1 (
    .in0(and_5_out), .in1(or_4_out), .in2(xor_2_out), .in3({ROR_Cin, A[7:1]}), .out(multiplexer_1_out),
    .sel(Opcode[3:2]));
  Multiplexer #(.width(8)) multiplexer_2 (
    .in0(adder_1_out), .in1(multiplexer_1_out), .out({NF_out, Result[6:0]}), .sel(Opcode[5]));
  not not_2 (not_2_out, A[7]);
  not not_3 (not_3_out, B[7]);
  not not_4 (not_4_out, NF_out);
  not not_5 (not_5_out, Opcode[2]);
  and and_6 (and_6_out, A[0], ALU_SHR_ROR);
  and and_7 (and_7_out, Adder_Cout, not_6_out);
  not not_6 (not_6_out, Opcode[4]);
  and and_8 (and_8_out, not_2_out, not_3_out, NF_out, not_5_out);
  and and_9 (and_9_out, A[7], B[7], not_4_out, not_5_out);
  and and_10 (and_10_out, not_2_out, B[7], NF_out, Opcode[2]);
  and and_11 (and_11_out, A[7], not_3_out, not_4_out, Opcode[2]);
  nor nor_1 (ZF_out, Result[0], Result[1], Result[2], Result[3], Result[4], Result[5], Result[6], NF_out);
  or or_5 (CF_out, and_6_out, and_7_out);
  or or_6 (OF_out, and_8_out, and_9_out, and_10_out, and_11_out);

  assign Result[7] = NF_out;

  // Other names for the same wires on the sheet: ALU_A[7:0] = A; SHR_Cout = A[0]; ALU_B[7:0] = B; ALU_CF = CF_out;
  //   ALU_OF = OF_out; ALU_out[7:0] = {NF_out, Result[6:0]}; ALU_NF = NF_out; ALU_ZF = ZF_out; S_CF = CF_in
endmodule

module Bin_to_BCD_16 (
  input  [15:0] Bin,
  output [3:0] Out_1,
  output [3:0] Out_10,
  output [3:0] Out_100,
  output [3:0] Out_1000,
  output [3:0] Out_10000
);

  wire [15:0] divider_1_out, divider_2_out, divider_3_out, divider_4_out;
  wire [15:4] divider_1_rem, divider_2_rem, divider_3_rem, divider_4_rem, divider_5_rem;

  Divider #(.width(16)) divider_1 (
    .a(Bin), .b(16'ha), .out(divider_1_out), .rem({divider_1_rem, Out_1}));  // open: upper
  Divider #(.width(16)) divider_2 (
    .a(divider_1_out), .b(16'ha), .out(divider_2_out), .rem({divider_2_rem, Out_10}));  // open: upper
  Divider #(.width(16)) divider_3 (
    .a(divider_2_out), .b(16'ha), .out(divider_3_out), .rem({divider_3_rem, Out_100}));  // open: upper
  Divider #(.width(16)) divider_4 (
    .a(divider_3_out), .b(16'ha), .out(divider_4_out), .rem({divider_4_rem, Out_1000}));  // open: upper
  Divider #(.width(16)) divider_5 (.a(divider_4_out), .b(16'ha), .rem({divider_5_rem, Out_10000}));  // open: out, upper
endmodule

module LED_Matrix_Driver (
  input  [7:0] Data,
  input  Data_en,
  input  Start_data,
  input  Stop_data,
  input  Reset,
  output [7:0] Row_0,
  output [7:0] Row_1,
  output [7:0] Row_2,
  output [7:0] Row_3,
  output [7:0] Row_4,
  output [7:0] Row_5,
  output [7:0] Row_6,
  output [7:0] Row_7
);

  wire and_1_out, clock_1_out, clock_2_out, s_r_ff_1_q, Visible;
  wire [7:0] bit_extender_1_out, shift_register_1_q0, shift_register_1_q1, shift_register_1_q2,
       shift_register_1_q3, shift_register_1_q4, shift_register_1_q5, shift_register_1_q6,
       shift_register_1_q7;

  S_R_Flip_Flop s_r_ff_1 (
    .S(Start_data), .R(Stop_data), .clk(clock_1_out), .Q(s_r_ff_1_q), .reset(Reset), .Qn(Visible));  // open: preset
  Clock clock_1 (.out(clock_1_out));
  and and_1 (and_1_out, Data_en, s_r_ff_1_q);
  Shift_Register shift_register_1 (
    .shift(and_1_out), .in(Data[0]), .clk(clock_2_out), .clr(Reset), .q0(shift_register_1_q0[0]),
    .q1(shift_register_1_q1[0]), .q2(shift_register_1_q2[0]), .q3(shift_register_1_q3[0]),
    .q4(shift_register_1_q4[0]), .q5(shift_register_1_q5[0]), .q6(shift_register_1_q6[0]),
    .q7(shift_register_1_q7[0]));  // open: out, load, d0, d1, d2, d3, d4, d5, d6, d7
  Shift_Register shift_register_2 (
    .shift(and_1_out), .in(Data[1]), .clk(clock_2_out), .clr(Reset), .q0(shift_register_1_q0[1]),
    .q1(shift_register_1_q1[1]), .q2(shift_register_1_q2[1]), .q3(shift_register_1_q3[1]),
    .q4(shift_register_1_q4[1]), .q5(shift_register_1_q5[1]), .q6(shift_register_1_q6[1]),
    .q7(shift_register_1_q7[1]));  // open: out, load, d0, d1, d2, d3, d4, d5, d6, d7
  Shift_Register shift_register_3 (
    .shift(and_1_out), .in(Data[2]), .clk(clock_2_out), .clr(Reset), .q0(shift_register_1_q0[2]),
    .q1(shift_register_1_q1[2]), .q2(shift_register_1_q2[2]), .q3(shift_register_1_q3[2]),
    .q4(shift_register_1_q4[2]), .q5(shift_register_1_q5[2]), .q6(shift_register_1_q6[2]),
    .q7(shift_register_1_q7[2]));  // open: out, load, d0, d1, d2, d3, d4, d5, d6, d7
  Shift_Register shift_register_4 (
    .shift(and_1_out), .in(Data[3]), .clk(clock_2_out), .clr(Reset), .q0(shift_register_1_q0[3]),
    .q1(shift_register_1_q1[3]), .q2(shift_register_1_q2[3]), .q3(shift_register_1_q3[3]),
    .q4(shift_register_1_q4[3]), .q5(shift_register_1_q5[3]), .q6(shift_register_1_q6[3]),
    .q7(shift_register_1_q7[3]));  // open: out, load, d0, d1, d2, d3, d4, d5, d6, d7
  Shift_Register shift_register_5 (
    .shift(and_1_out), .in(Data[4]), .clk(clock_2_out), .clr(Reset), .q0(shift_register_1_q0[4]),
    .q1(shift_register_1_q1[4]), .q2(shift_register_1_q2[4]), .q3(shift_register_1_q3[4]),
    .q4(shift_register_1_q4[4]), .q5(shift_register_1_q5[4]), .q6(shift_register_1_q6[4]),
    .q7(shift_register_1_q7[4]));  // open: out, load, d0, d1, d2, d3, d4, d5, d6, d7
  Shift_Register shift_register_6 (
    .shift(and_1_out), .in(Data[5]), .clk(clock_2_out), .clr(Reset), .q0(shift_register_1_q0[5]),
    .q1(shift_register_1_q1[5]), .q2(shift_register_1_q2[5]), .q3(shift_register_1_q3[5]),
    .q4(shift_register_1_q4[5]), .q5(shift_register_1_q5[5]), .q6(shift_register_1_q6[5]),
    .q7(shift_register_1_q7[5]));  // open: out, load, d0, d1, d2, d3, d4, d5, d6, d7
  Shift_Register shift_register_7 (
    .shift(and_1_out), .in(Data[6]), .clk(clock_2_out), .clr(Reset), .q0(shift_register_1_q0[6]),
    .q1(shift_register_1_q1[6]), .q2(shift_register_1_q2[6]), .q3(shift_register_1_q3[6]),
    .q4(shift_register_1_q4[6]), .q5(shift_register_1_q5[6]), .q6(shift_register_1_q6[6]),
    .q7(shift_register_1_q7[6]));  // open: out, load, d0, d1, d2, d3, d4, d5, d6, d7
  Shift_Register shift_register_8 (
    .shift(and_1_out), .in(Data[7]), .clk(clock_2_out), .clr(Reset), .q0(shift_register_1_q0[7]),
    .q1(shift_register_1_q1[7]), .q2(shift_register_1_q2[7]), .q3(shift_register_1_q3[7]),
    .q4(shift_register_1_q4[7]), .q5(shift_register_1_q5[7]), .q6(shift_register_1_q6[7]),
    .q7(shift_register_1_q7[7]));  // open: out, load, d0, d1, d2, d3, d4, d5, d6, d7
  Clock clock_2 (.out(clock_2_out));
  assign bit_extender_1_out = {{7{Visible}}, Visible};  // Bit_Extender bit_extender_1
  assign Row_0 = shift_register_1_q7 & bit_extender_1_out;  // AND_Gate and_2, 8 bits wide
  assign Row_1 = shift_register_1_q6 & bit_extender_1_out;  // AND_Gate and_3, 8 bits wide
  assign Row_2 = shift_register_1_q5 & bit_extender_1_out;  // AND_Gate and_4, 8 bits wide
  assign Row_3 = shift_register_1_q4 & bit_extender_1_out;  // AND_Gate and_5, 8 bits wide
  assign Row_4 = shift_register_1_q3 & bit_extender_1_out;  // AND_Gate and_6, 8 bits wide
  assign Row_5 = shift_register_1_q2 & bit_extender_1_out;  // AND_Gate and_7, 8 bits wide
  assign Row_6 = shift_register_1_q1 & bit_extender_1_out;  // AND_Gate and_8, 8 bits wide
  assign Row_7 = shift_register_1_q0 & bit_extender_1_out;  // AND_Gate and_9, 8 bits wide
endmodule
