// Logisim project PFC_mini_v3_74xx.circ as structural Verilog: 14 circuits, main circuit main
module main (
  input  Start,
  input  Reset
);

  wire ALU_En, ALU_En_ROM, alu_module_1_cf_out, alu_module_1_nf_out, alu_module_1_of_out,
       alu_module_1_zf_out, and_1_out, and_2_out, and_3_out, and_4_out, and_5_out, and_6_out, and_7_out,
       clock_1_out, clock_2_out, clock_5_out, clock_7_out, clock_8_out, Execute_1, Execute_2, Fetch_1,
       Fetch_2, Idle, Length_2, MMIO, n7400_1_pin3, n7400_1_pin5, n7400_1_pin6, n7400_1_pin10, n7400_2_pin3,
       n7400_3_pin1, n7400_3_pin3, n7400_3_pin11, n7404_1_pin12, n7410_1_pin1, n7410_1_pin8, n7410_1_pin9,
       n7410_1_pin12, n7410_2_pin6, n7410_2_pin8, n7430_1_pin11, n7430_1_pin12, n7432_1_pin3, n7432_1_pin6,
       n7432_1_pin8, n7432_1_pin11, n7486_1_pin11, n74138_1_pin4, n74138_1_pin5, n74138_1_pin6,
       n74138_1_pin7, n74138_1_pin9, n74138_2_pin4, n74138_2_pin6, n74138_3_pin4, n74138_3_pin6,
       n74138_4_pin4, n74138_4_pin6, n74139_1_pin1, n74139_2_pin1, n74151_1_pin1, n74151_1_pin2,
       n74151_1_pin5, n74151_1_pin7, n74151_1_pin14, n74153_1_pin1, n74153_1_pin9, n74541_1_pin19,
       n74541_2_pin19, n74541_3_pin19, n74541_4_pin19, n_ADDR_A, n_ADDR_B, n_ADDR_C, n_ADDR_D, n_ADDR_Opnd,
       n_Execute_1, n_Execute_2, n_Fetch_1, n_Fetch_2, n_Halt, n_Idle, n_In_0_En, n_In_1_En, n_In_2_En,
       n_In_3_En, n_JMP, n_JMP_Cond, n_Jump_En, n_MMIO, n_RAM_OE, n_RAM_WE, n_RD_A, n_RD_B, n_RD_C, n_RD_D,
       n_RD_Opnd, n_WR_A, n_WR_B, n_WR_C, n_WR_D, n_WR_RAM, not_1_out, not_2_out, not_3_out, not_4_out,
       not_5_out, not_6_out, not_7_out, not_8_out, not_9_out, not_10_out, not_11_out, or_1_out, random_1_p2,
       Set_CF, Set_CF_ROM, Set_OF, Set_OF_ROM, status_flags_module_1_cf_out, status_flags_module_1_nf_out,
       status_flags_module_1_of_out, status_flags_module_1_zf_out, ttl_74175_1_nq1, ttl_74175_1_nq2,
       ttl_74175_1_nq3, ttl_74175_1_q1, ttl_74175_1_q2, ttl_74175_1_q3, WR_MAR;
  wire [1:0] Control;
  wire [2:0] ADDR, RD, WR;
  wire [3:0] bin_to_bcd_16_1_out_1, bin_to_bcd_16_1_out_10, bin_to_bcd_16_1_out_100,
       bin_to_bcd_16_1_out_1000, bin_to_bcd_16_1_out_10000, Buttons;
  wire [7:0] A_reg_out, Address_bus, ALU_out, B_reg_out, C_reg_out, D_reg_out, Data_bus, In_0, In_1, In_2,
       In_3, led_matrix_driver_1_row_0, led_matrix_driver_1_row_1, led_matrix_driver_1_row_2,
       led_matrix_driver_1_row_3, led_matrix_driver_1_row_4, led_matrix_driver_1_row_5,
       led_matrix_driver_1_row_6, led_matrix_driver_1_row_7, MAR_reg_out, mux_2_to_1_8_bit_module_1_y,
       Opcode, Operand, PC_pc_out, Program_out, register_2_q;
  wire [15:0] register_3_q;

  Mux_2_to_1_8_bit_Module mux_2_to_1_8_bit_module_1 (
    .B(Opcode), .Sel(n_Fetch_1), .A(Program_out), .Y(mux_2_to_1_8_bit_module_1_y));
  ROM uCode_ROM_1 (.addr(mux_2_to_1_8_bit_module_1_y), .data({RD, WR, WR_MAR, Length_2}));
  ROM uCode_ROM_2 (.addr(mux_2_to_1_8_bit_module_1_y), .data({Control, Set_OF_ROM, Set_CF_ROM, ALU_En_ROM, ADDR}));
  TTL_74175 ttl_74175_1 (
    .CLK(clock_1_out), .nCLR(n7410_2_pin6), .D1(n74151_1_pin5), .D2(n7410_1_pin12), .D3(n7410_1_pin8),
    .Q1(ttl_74175_1_q1), .nQ1(ttl_74175_1_nq1), .Q2(ttl_74175_1_q2), .nQ2(ttl_74175_1_nq2),
    .Q3(ttl_74175_1_q3), .nQ3(ttl_74175_1_nq3));  // open: D4, Q4, nQ4
  _7410 u_7410_1 (
    .pin1(n7410_1_pin1), .pin2(n7410_1_pin1), .pin3(ttl_74175_1_q1), .pin4(ttl_74175_1_nq3), .pin5(Length_2),
    .pin6(n7410_1_pin1), .pin13(n7410_1_pin1), .pin12(n7410_1_pin12), .pin11(ttl_74175_1_nq1),
    .pin10(ttl_74175_1_nq2), .pin9(n7410_1_pin9), .pin8(n7410_1_pin8));
  Clock clock_1 (.out(clock_1_out));
  _74138 u_74138_1 (
    .pin1(ttl_74175_1_q1), .pin2(ttl_74175_1_q2), .pin3(ttl_74175_1_q3), .pin4(n74138_1_pin4),
    .pin5(n74138_1_pin5), .pin6(n74138_1_pin6), .pin7(n74138_1_pin7), .pin15(n_Idle), .pin14(n_Fetch_1),
    .pin11(n_Execute_2), .pin10(n_Execute_1), .pin9(n74138_1_pin9));  // open: pin13, pin12
  _74151 u_74151_1 (
    .pin1(n74151_1_pin1), .pin2(n74151_1_pin2), .pin3(WR_MAR), .pin4(Start), .pin5(n74151_1_pin5),
    .pin7(n74151_1_pin7), .pin15(n_Halt), .pin14(n74151_1_pin14), .pin13(WR_MAR), .pin12(WR_MAR),
    .pin11(ttl_74175_1_q1), .pin10(ttl_74175_1_q2), .pin9(ttl_74175_1_q3));  // open: pin6
  _7408 u_7408_1 (
    .pin13(n74138_1_pin7), .pin12(n74138_1_pin9), .pin11(n_Fetch_2));  // open: pin1, pin2, pin3, pin4, pin5, pin6, pin10, pin9, pin8
  _74138 u_74138_2 (
    .pin1(WR[0]), .pin2(WR[1]), .pin3(WR[2]), .pin4(n74138_2_pin4), .pin5(n_Execute_2), .pin6(n74138_2_pin6),
    .pin7(n_WR_D), .pin14(n_WR_RAM), .pin11(n_WR_A), .pin10(n_WR_B), .pin9(n_WR_C));  // open: pin15, pin13, pin12
  _74138 u_74138_3 (
    .pin1(RD[0]), .pin2(RD[1]), .pin3(RD[2]), .pin4(n74138_3_pin4), .pin5(n_Execute_2), .pin6(n74138_3_pin6),
    .pin7(n_RD_D), .pin14(n_RAM_OE), .pin13(n_RD_Opnd), .pin11(n_RD_A), .pin10(n_RD_B), .pin9(n_RD_C));  // open: pin15, pin12
  _74138 u_74138_4 (
    .pin1(ADDR[0]), .pin2(ADDR[1]), .pin3(ADDR[2]), .pin4(n74138_4_pin4), .pin5(n_Execute_1),
    .pin6(n74138_4_pin6), .pin7(n_ADDR_D), .pin14(n_ADDR_Opnd), .pin11(n_ADDR_A), .pin10(n_ADDR_B),
    .pin9(n_ADDR_C));  // open: pin15, pin13, pin12
  _74139 u_74139_1 (
    .pin1(n74139_1_pin1), .pin15(n_Execute_2), .pin14(Control[0]), .pin13(Control[1]), .pin11(n_JMP),
    .pin10(n_JMP_Cond), .pin9(n_Halt));  // open: pin2, pin3, pin4, pin5, pin6, pin7, pin12
  _7404 u_7404_1 (
    .pin13(n_Execute_2), .pin12(n7404_1_pin12));  // open: pin1, pin2, pin3, pin4, pin5, pin6, pin11, pin10, pin9, pin8
  _7408 u_7408_2 (
    .pin1(ALU_En_ROM), .pin2(n7404_1_pin12), .pin3(ALU_En), .pin13(Set_CF_ROM), .pin12(n7404_1_pin12),
    .pin11(Set_CF), .pin10(Set_OF_ROM), .pin9(n7404_1_pin12), .pin8(Set_OF));  // open: pin4, pin5, pin6
  _7410 u_7410_2 (
    .pin3(Reset), .pin4(Reset), .pin5(Reset), .pin6(n7410_2_pin6), .pin11(n_Fetch_1), .pin10(n_Fetch_2),
    .pin9(n_Jump_En), .pin8(n7410_2_pin8));  // open: pin1, pin2, pin13, pin12
  Clock clock_2 (.out(clock_2_out));
  Register_Module u_Opcode (
    .n_Write_en(n_Fetch_1), .Reset(Reset), .CLK(clock_2_out), .Data_in(Program_out), .Reg_out(Opcode));
  PC_Module PC (
    .Count_en(n7410_2_pin8), .CLK(clock_2_out), .n_Reset(n7410_2_pin6), .n_Jump_en(n_Jump_En),
    .Jump_addr(Operand), .PC_out(PC_pc_out));
  Register_Module u_Operand (
    .n_Write_en(n_Fetch_2), .Reset(Reset), .CLK(clock_2_out), .Data_in(Program_out), .Reg_out(Operand));
  Accumulator_Module A (
    .ALU_in(ALU_out), .Sel_in(ALU_En), .n_Write_en(n_WR_A), .Reset(Reset), .CLK(clock_2_out),
    .Data_in(Data_bus), .Reg_out(A_reg_out));
  Register_Module B (.n_Write_en(n_WR_B), .Reset(Reset), .CLK(clock_2_out), .Data_in(Data_bus), .Reg_out(B_reg_out));
  Register_Module C (.n_Write_en(n_WR_C), .Reset(Reset), .CLK(clock_2_out), .Data_in(Data_bus), .Reg_out(C_reg_out));
  Register_Module D (.n_Write_en(n_WR_D), .Reset(Reset), .CLK(clock_2_out), .Data_in(Data_bus), .Reg_out(D_reg_out));
  ROM Program_Memory (.addr(PC_pc_out), .data(Program_out));
  Register_Tri_State_Module register_tri_state_module_1 (
    .n_Data_en(n_RD_Opnd), .n_Addr_en(n_ADDR_Opnd), .Reg_in(Operand), .Data(Data_bus), .Addr(Address_bus));
  Register_Tri_State_Module register_tri_state_module_2 (
    .n_Data_en(n_RD_A), .n_Addr_en(n_ADDR_A), .Reg_in(A_reg_out), .Data(Data_bus), .Addr(Address_bus));
  Register_Tri_State_Module register_tri_state_module_3 (
    .n_Data_en(n_RD_B), .n_Addr_en(n_ADDR_B), .Reg_in(B_reg_out), .Data(Data_bus), .Addr(Address_bus));
  Register_Tri_State_Module register_tri_state_module_4 (
    .n_Data_en(n_RD_C), .n_Addr_en(n_ADDR_C), .Reg_in(C_reg_out), .Data(Data_bus), .Addr(Address_bus));
  Register_Tri_State_Module register_tri_state_module_5 (
    .n_Data_en(n_RD_D), .n_Addr_en(n_ADDR_D), .Reg_in(D_reg_out), .Data(Data_bus), .Addr(Address_bus));
  Pull_Resistor pull_resistor_1 (.node(Data_bus));
  Pull_Resistor pull_resistor_2 (.node(Address_bus));
  Register_Module MAR (
    .n_Write_en(n_Execute_1), .Reset(Reset), .CLK(clock_2_out), .Data_in(Address_bus), .Reg_out(MAR_reg_out));
  ALU_Module alu_module_1 (
    .Opcode(Opcode), .A(A_reg_out), .B(Data_bus), .CF_in(status_flags_module_1_cf_out), .Result(ALU_out),
    .ZF_out(alu_module_1_zf_out), .NF_out(alu_module_1_nf_out), .CF_out(alu_module_1_cf_out),
    .OF_out(alu_module_1_of_out));
  Status_Flags_Module status_flags_module_1 (
    .ZF_in(alu_module_1_zf_out), .NF_in(alu_module_1_nf_out), .CF_in(alu_module_1_cf_out),
    .OF_in(alu_module_1_of_out), .ALU_en(ALU_En), .Set_CF(Set_CF), .Set_OF(Set_OF), .Reset(Reset),
    .CLK(clock_2_out), .ZF_out(status_flags_module_1_zf_out), .NF_out(status_flags_module_1_nf_out),
    .CF_out(status_flags_module_1_cf_out), .OF_out(status_flags_module_1_of_out));
  _7432 u_7432_1 (
    .pin1(n_In_2_En), .pin2(n_RAM_OE), .pin3(n7432_1_pin3), .pin4(n_In_3_En), .pin5(n_RAM_OE),
    .pin6(n7432_1_pin6), .pin13(n_In_0_En), .pin12(n_RAM_OE), .pin11(n7432_1_pin11), .pin10(n_In_1_En),
    .pin9(n_RAM_OE), .pin8(n7432_1_pin8));
  not not_1 (not_1_out, n_RAM_WE);
  not not_2 (not_2_out, n_RAM_OE);
  and and_1 (and_1_out, not_2_out, not_3_out);
  not not_3 (not_3_out, MMIO);
  _7430 u_7430_1 (
    .pin1(MAR_reg_out[2]), .pin2(MAR_reg_out[3]), .pin3(MAR_reg_out[4]), .pin4(MAR_reg_out[5]),
    .pin5(MAR_reg_out[6]), .pin6(MAR_reg_out[7]), .pin12(n7430_1_pin12), .pin11(n7430_1_pin11), .pin8(n_MMIO));  // open: pin13, pin10, pin9
  RAM #(.databus("bidir"), .enables("line"), .trigger("high")) Data_Memory (
    .addr(MAR_reg_out), .data(Data_bus));  // open: we, oe, clk
  _74153 u_74153_1 (
    .pin1(n74153_1_pin1), .pin2(Opcode[1]), .pin15(n74153_1_pin1), .pin14(Opcode[0]),
    .pin13(status_flags_module_1_of_out), .pin12(status_flags_module_1_cf_out),
    .pin11(status_flags_module_1_nf_out), .pin10(status_flags_module_1_zf_out), .pin9(n74153_1_pin9));  // open: pin3, pin4, pin5, pin6, pin7
  _7400 u_7400_1 (
    .pin1(n_WR_RAM), .pin2(n_WR_RAM), .pin3(n7400_1_pin3), .pin4(n7400_1_pin3), .pin5(n7400_1_pin5),
    .pin6(n7400_1_pin6), .pin13(n_MMIO), .pin12(n_MMIO), .pin11(MMIO), .pin10(n7400_1_pin10),
    .pin9(n7400_1_pin10), .pin8(n7400_1_pin5));
  _74139 u_74139_2 (
    .pin1(n74139_2_pin1), .pin15(n_MMIO), .pin14(MAR_reg_out[0]), .pin13(MAR_reg_out[1]), .pin12(n_In_0_En),
    .pin11(n_In_1_En), .pin10(n_In_2_En), .pin9(n_In_3_En));  // open: pin2, pin3, pin4, pin5, pin6, pin7
  _74541 u_74541_1 (
    .pin1(n7432_1_pin11), .pin2(In_0[0]), .pin3(In_0[1]), .pin4(In_0[2]), .pin5(In_0[3]), .pin6(In_0[4]),
    .pin7(In_0[5]), .pin8(In_0[6]), .pin9(In_0[7]), .pin19(n74541_1_pin19), .pin18(Data_bus[0]),
    .pin17(Data_bus[1]), .pin16(Data_bus[2]), .pin15(Data_bus[3]), .pin14(Data_bus[4]), .pin13(Data_bus[5]),
    .pin12(Data_bus[6]), .pin11(Data_bus[7]));
  _74541 u_74541_2 (
    .pin1(n7432_1_pin8), .pin2(In_1[0]), .pin3(In_1[1]), .pin4(In_1[2]), .pin5(In_1[3]), .pin6(In_1[4]),
    .pin7(In_1[5]), .pin8(In_1[6]), .pin9(In_1[7]), .pin19(n74541_2_pin19), .pin18(Data_bus[0]),
    .pin17(Data_bus[1]), .pin16(Data_bus[2]), .pin15(Data_bus[3]), .pin14(Data_bus[4]), .pin13(Data_bus[5]),
    .pin12(Data_bus[6]), .pin11(Data_bus[7]));
  _74541 u_74541_3 (
    .pin1(n7432_1_pin3), .pin2(In_2[0]), .pin3(In_2[1]), .pin4(In_2[2]), .pin5(In_2[3]), .pin6(In_2[4]),
    .pin7(In_2[5]), .pin8(In_2[6]), .pin9(In_2[7]), .pin19(n74541_3_pin19), .pin18(Data_bus[0]),
    .pin17(Data_bus[1]), .pin16(Data_bus[2]), .pin15(Data_bus[3]), .pin14(Data_bus[4]), .pin13(Data_bus[5]),
    .pin12(Data_bus[6]), .pin11(Data_bus[7]));
  _74541 u_74541_4 (
    .pin1(n7432_1_pin6), .pin2(In_3[0]), .pin3(In_3[1]), .pin4(In_3[2]), .pin5(In_3[3]), .pin6(In_3[4]),
    .pin7(In_3[5]), .pin8(In_3[6]), .pin9(In_3[7]), .pin19(n74541_4_pin19), .pin18(Data_bus[0]),
    .pin17(Data_bus[1]), .pin16(Data_bus[2]), .pin15(Data_bus[3]), .pin14(Data_bus[4]), .pin13(Data_bus[5]),
    .pin12(Data_bus[6]), .pin11(Data_bus[7]));
  Clock clock_3 (.out(n7400_1_pin10));
  _7486 u_7486_1 (
    .pin13(Opcode[2]), .pin12(n74153_1_pin9), .pin11(n7486_1_pin11));  // open: pin1, pin2, pin3, pin4, pin5, pin6, pin10, pin9, pin8
  _7400 u_7400_2 (
    .pin1(n7400_1_pin6), .pin2(n7400_1_pin6), .pin3(n7400_2_pin3), .pin4(n7400_2_pin3), .pin5(n_MMIO),
    .pin6(n_RAM_WE));  // open: pin13, pin12, pin11, pin10, pin9, pin8
  _7400 u_7400_3 (
    .pin1(n7400_3_pin1), .pin2(n_JMP), .pin3(n7400_3_pin3), .pin4(n7400_3_pin3), .pin5(n7400_3_pin3),
    .pin6(n_Jump_En), .pin13(n_JMP_Cond), .pin12(n_JMP_Cond), .pin11(n7400_3_pin11), .pin10(n7400_3_pin11),
    .pin9(n7486_1_pin11), .pin8(n7400_3_pin1));
  Clock clock_4 ();  // open: out
  not not_4 (not_4_out, n_In_1_En);
  and and_2 (and_2_out, not_4_out, not_5_out);
  not not_5 (not_5_out, n_WR_RAM);
  not not_6 (not_6_out, n_In_0_En);
  and and_3 (and_3_out, not_6_out, not_7_out);
  not not_7 (not_7_out, n_WR_RAM);
  and and_4 (and_4_out, Data_bus[0], and_2_out);
  and and_5 (and_5_out, Data_bus[1], and_2_out);
  LED led_1 (.in(Idle));
  LED led_2 (.in(Fetch_1));
  LED led_3 (.in(Fetch_2));
  LED led_4 (.in(Execute_1));
  LED led_5 (.in(Execute_2));
  DotMatrix #(.dotshape("circle"), .inputtype("row"), .matrixcols(8), .matrixrows(8), .persist(300)) dotmatrix_1 (
    .row0(led_matrix_driver_1_row_0), .row1(led_matrix_driver_1_row_1), .row2(led_matrix_driver_1_row_2),
    .row3(led_matrix_driver_1_row_3), .row4(led_matrix_driver_1_row_4), .row5(led_matrix_driver_1_row_5),
    .row6(led_matrix_driver_1_row_6), .row7(led_matrix_driver_1_row_7));
  LED_Matrix_Driver led_matrix_driver_1 (
    .Data(Data_bus), .Data_en(and_3_out), .Start_data(and_4_out), .Stop_data(and_5_out), .Reset(Reset),
    .Row_7(led_matrix_driver_1_row_7), .Row_0(led_matrix_driver_1_row_0), .Row_1(led_matrix_driver_1_row_1),
    .Row_2(led_matrix_driver_1_row_2), .Row_3(led_matrix_driver_1_row_3), .Row_4(led_matrix_driver_1_row_4),
    .Row_5(led_matrix_driver_1_row_5), .Row_6(led_matrix_driver_1_row_6));
  Button button_1 (.out(Buttons[3]));
  Register #(.width(4)) register_1 (.D(Buttons), .en(or_1_out), .clk(clock_5_out), .Q(In_0[3:0]), .clr(Reset));
  or or_1 (or_1_out, Buttons[0], Buttons[1], Buttons[2], Buttons[3]);
  Clock clock_5 (.out(clock_5_out));
  Button button_2 (.out(Buttons[0]));
  Button button_3 (.out(Buttons[2]));
  Button button_4 (.out(Buttons[1]));
  // Random random_1: pin names not known; wires that end beside it: 1'b1, random_1_p2
  Clock clock_6 (.out(random_1_p2));
  _7404 u_7404_2 (
    .pin1(n_Execute_1), .pin2(Execute_1), .pin3(n_Execute_2), .pin4(Execute_2), .pin13(n_Fetch_2),
    .pin12(Fetch_2), .pin11(n_Fetch_1), .pin10(Fetch_1), .pin9(n_Idle), .pin8(Idle));  // open: pin5, pin6
  Hex_Digit_Display hex_digit_display_1 (.value(bin_to_bcd_16_1_out_10000));  // open: dp
  Hex_Digit_Display hex_digit_display_2 (.value(bin_to_bcd_16_1_out_1000));  // open: dp
  Hex_Digit_Display hex_digit_display_3 (.value(bin_to_bcd_16_1_out_100));  // open: dp
  Bin_to_BCD_16 bin_to_bcd_16_1 (
    .Bin(register_3_q), .Out_1(bin_to_bcd_16_1_out_1), .Out_10(bin_to_bcd_16_1_out_10),
    .Out_100(bin_to_bcd_16_1_out_100), .Out_1000(bin_to_bcd_16_1_out_1000),
    .Out_10000(bin_to_bcd_16_1_out_10000));
  Register register_2 (.D(Data_bus), .en(and_6_out), .clk(clock_7_out), .Q(register_2_q));  // open: clr
  not not_8 (not_8_out, n_WR_RAM);
  and and_6 (and_6_out, not_8_out, not_9_out);
  not not_9 (not_9_out, n_In_0_En);
  Clock clock_7 (.out(clock_7_out));
  not not_10 (not_10_out, n_WR_RAM);
  and and_7 (and_7_out, not_10_out, not_11_out);
  not not_11 (not_11_out, n_In_1_En);
  Hex_Digit_Display hex_digit_display_4 (.value(bin_to_bcd_16_1_out_10));  // open: dp
  Hex_Digit_Display hex_digit_display_5 (.value(bin_to_bcd_16_1_out_1));  // open: dp
  Register #(.width(16)) register_3 (
    .D({Data_bus, register_2_q}), .en(and_7_out), .clk(clock_8_out), .Q(register_3_q));  // open: clr
  Clock clock_8 (.out(clock_8_out));
  // also tied to GND on the sheet: {n74151_1_pin1, n74151_1_pin2, n74151_1_pin14, n74138_1_pin4, n74138_1_pin5, n74151_1_pin7, n74139_1_pin1, n74138_2_pin4, n74138_3_pin4, n74138_4_pin4, n74153_1_pin1, n74541_1_pin19, n74541_2_pin19, n74541_3_pin19, n74541_4_pin19, n74139_2_pin1, In_0[4], In_0[5], In_0[6], In_0[7]}
  // also tied to VCC on the sheet: {n7410_1_pin9, n74138_1_pin6, n74138_2_pin6, n74138_3_pin6, n74138_4_pin6, n7430_1_pin12, n7430_1_pin11}

  // Other names for the same wires on the sheet: n_RAM_CS = MMIO; n_RD_RAM = n_RAM_OE

  // Notes on the sheet:
  //   contents of uCode_ROM_1 (hex, n*v repeats v):
  //   90 b0 d0 f0 94 b4 d4 f4 98 b8 d8 f8 9c bc dc fc 4*51 4*55 4*59 4*5d 16*0 16*1 4*86 4*a6 4*c6 4*e6
  //   4*87 4*a7 4*c7 4*e7 4*32 4*36 4*3a 4*3e 4*33 4*37 4*3b 4*3f 90 b0 d0 f0 90 b0 d0 f0 90 b0 d0 f0 90
  //   b0 d0 f0 16*51 90 b0 d0 f0 90 b0 d0 f0 90 b0 d0 f0 4*10 12*51 4*10 4*0 80 a0 c0 e0 12*0 4*41 8*0 80
  //   a0 c0 e0 12*0 4*41
  //   contents of uCode_ROM_2 (hex, n*v repeats v):
  //   40*0 8*c0 8*40 8*80 4 5 6 7 4 5 6 7 4 5 6 7 4 5 6 7 16*1 4 5 6 7 4 5 6 7 4 5 6 7 4 5 6 7 16*1 32*38
  //   12*8 4*18 12*8 4*18 4*0 4*38 12*0 4*38 8*0 4*8 12*0 4*8
  //   contents of Program_Memory (hex, n*v repeats v):
  //   10 8 14 1 18 0 94 1 39 15 44 c 90 20 48 1 80 4 3 30 6 10 4 50 10 10 40 50 11 10 1b 50 13 70 fd b0 3f
  //   50 12 30 98 70 fc d4 0 38 31 50 10 74 40 1 b0 38 ac ac ac 90 20 c 1 b0 7 60 b8 ff 67 a1 43 70 11 68
  //   74 10 1 b0 1 38 54 2 94 8 30 73 1 b0 2 38 5e 2 90 8 30 73 1 b0 4 38 68 2 90 1 30 6b 2 94 1 b0 7 4 2
  //   b0 38 30 79 b0 38 4 2 b0 7 a5 50 13 74 12 c5 3c 89 70 11 90 1 50 11 30 21 10 40 18 1 82 64 86 44 82
  //   4 94 7f 1 3c 8d 70 13 74 11 41 4 b0 38 ac ac ac 90 20 c 1 b0 7 64 63 a5 43 74 12 1 b0 38 ac ac ac 90
  //   20 c 1 b0 7 64 63 a5 43 10 1 50 fd 10 20 64 54 fc 90 1 d4 28 3c c5 10 2 50 fd 30 29 28
endmodule

module Bin_to_BCD_16 (
  input  [15:0] Bin,
  output [3:0] Out_1,
  output [3:0] Out_10,
  output [3:0] Out_100,
  output [3:0] Out_1000,
  output [3:0] Out_10000
);

  wire [15:0] divider_1_out, divider_2_out, divider_3_out, divider_4_out;
  wire [15:4] divider_1_rem, divider_2_rem, divider_3_rem, divider_4_rem, divider_5_rem;

  Divider #(.width(16)) divider_1 (
    .a(Bin), .b(16'ha), .out(divider_1_out), .rem({divider_1_rem, Out_1}));  // open: upper
  Divider #(.width(16)) divider_2 (
    .a(divider_1_out), .b(16'ha), .out(divider_2_out), .rem({divider_2_rem, Out_10}));  // open: upper
  Divider #(.width(16)) divider_3 (
    .a(divider_2_out), .b(16'ha), .out(divider_3_out), .rem({divider_3_rem, Out_100}));  // open: upper
  Divider #(.width(16)) divider_4 (
    .a(divider_3_out), .b(16'ha), .out(divider_4_out), .rem({divider_4_rem, Out_1000}));  // open: upper
  Divider #(.width(16)) divider_5 (.a(divider_4_out), .b(16'ha), .rem({divider_5_rem, Out_10000}));  // open: out, upper
endmodule

module LED_Matrix_Driver (
  input  [7:0] Data,
  input  Data_en,
  input  Start_data,
  input  Stop_data,
  input  Reset,
  output [7:0] Row_0,
  output [7:0] Row_1,
  output [7:0] Row_2,
  output [7:0] Row_3,
  output [7:0] Row_4,
  output [7:0] Row_5,
  output [7:0] Row_6,
  output [7:0] Row_7
);

  wire and_1_out, clock_1_out, clock_2_out, s_r_ff_1_q, Visible;
  wire [7:0] bit_extender_1_out, shift_register_1_q0, shift_register_1_q1, shift_register_1_q2,
       shift_register_1_q3, shift_register_1_q4, shift_register_1_q5, shift_register_1_q6,
       shift_register_1_q7;

  S_R_Flip_Flop s_r_ff_1 (
    .S(Start_data), .R(Stop_data), .clk(clock_1_out), .Q(s_r_ff_1_q), .reset(Reset), .Qn(Visible));  // open: preset
  Clock clock_1 (.out(clock_1_out));
  and and_1 (and_1_out, Data_en, s_r_ff_1_q);
  Shift_Register shift_register_1 (
    .shift(and_1_out), .in(Data[0]), .clk(clock_2_out), .clr(Reset), .q0(shift_register_1_q0[0]),
    .q1(shift_register_1_q1[0]), .q2(shift_register_1_q2[0]), .q3(shift_register_1_q3[0]),
    .q4(shift_register_1_q4[0]), .q5(shift_register_1_q5[0]), .q6(shift_register_1_q6[0]),
    .q7(shift_register_1_q7[0]));  // open: out, load, d0, d1, d2, d3, d4, d5, d6, d7
  Shift_Register shift_register_2 (
    .shift(and_1_out), .in(Data[1]), .clk(clock_2_out), .clr(Reset), .q0(shift_register_1_q0[1]),
    .q1(shift_register_1_q1[1]), .q2(shift_register_1_q2[1]), .q3(shift_register_1_q3[1]),
    .q4(shift_register_1_q4[1]), .q5(shift_register_1_q5[1]), .q6(shift_register_1_q6[1]),
    .q7(shift_register_1_q7[1]));  // open: out, load, d0, d1, d2, d3, d4, d5, d6, d7
  Shift_Register shift_register_3 (
    .shift(and_1_out), .in(Data[2]), .clk(clock_2_out), .clr(Reset), .q0(shift_register_1_q0[2]),
    .q1(shift_register_1_q1[2]), .q2(shift_register_1_q2[2]), .q3(shift_register_1_q3[2]),
    .q4(shift_register_1_q4[2]), .q5(shift_register_1_q5[2]), .q6(shift_register_1_q6[2]),
    .q7(shift_register_1_q7[2]));  // open: out, load, d0, d1, d2, d3, d4, d5, d6, d7
  Shift_Register shift_register_4 (
    .shift(and_1_out), .in(Data[3]), .clk(clock_2_out), .clr(Reset), .q0(shift_register_1_q0[3]),
    .q1(shift_register_1_q1[3]), .q2(shift_register_1_q2[3]), .q3(shift_register_1_q3[3]),
    .q4(shift_register_1_q4[3]), .q5(shift_register_1_q5[3]), .q6(shift_register_1_q6[3]),
    .q7(shift_register_1_q7[3]));  // open: out, load, d0, d1, d2, d3, d4, d5, d6, d7
  Shift_Register shift_register_5 (
    .shift(and_1_out), .in(Data[4]), .clk(clock_2_out), .clr(Reset), .q0(shift_register_1_q0[4]),
    .q1(shift_register_1_q1[4]), .q2(shift_register_1_q2[4]), .q3(shift_register_1_q3[4]),
    .q4(shift_register_1_q4[4]), .q5(shift_register_1_q5[4]), .q6(shift_register_1_q6[4]),
    .q7(shift_register_1_q7[4]));  // open: out, load, d0, d1, d2, d3, d4, d5, d6, d7
  Shift_Register shift_register_6 (
    .shift(and_1_out), .in(Data[5]), .clk(clock_2_out), .clr(Reset), .q0(shift_register_1_q0[5]),
    .q1(shift_register_1_q1[5]), .q2(shift_register_1_q2[5]), .q3(shift_register_1_q3[5]),
    .q4(shift_register_1_q4[5]), .q5(shift_register_1_q5[5]), .q6(shift_register_1_q6[5]),
    .q7(shift_register_1_q7[5]));  // open: out, load, d0, d1, d2, d3, d4, d5, d6, d7
  Shift_Register shift_register_7 (
    .shift(and_1_out), .in(Data[6]), .clk(clock_2_out), .clr(Reset), .q0(shift_register_1_q0[6]),
    .q1(shift_register_1_q1[6]), .q2(shift_register_1_q2[6]), .q3(shift_register_1_q3[6]),
    .q4(shift_register_1_q4[6]), .q5(shift_register_1_q5[6]), .q6(shift_register_1_q6[6]),
    .q7(shift_register_1_q7[6]));  // open: out, load, d0, d1, d2, d3, d4, d5, d6, d7
  Shift_Register shift_register_8 (
    .shift(and_1_out), .in(Data[7]), .clk(clock_2_out), .clr(Reset), .q0(shift_register_1_q0[7]),
    .q1(shift_register_1_q1[7]), .q2(shift_register_1_q2[7]), .q3(shift_register_1_q3[7]),
    .q4(shift_register_1_q4[7]), .q5(shift_register_1_q5[7]), .q6(shift_register_1_q6[7]),
    .q7(shift_register_1_q7[7]));  // open: out, load, d0, d1, d2, d3, d4, d5, d6, d7
  Clock clock_2 (.out(clock_2_out));
  assign bit_extender_1_out = {{7{Visible}}, Visible};  // Bit_Extender bit_extender_1
  assign Row_0 = shift_register_1_q7 & bit_extender_1_out;  // AND_Gate and_2, 8 bits wide
  assign Row_1 = shift_register_1_q6 & bit_extender_1_out;  // AND_Gate and_3, 8 bits wide
  assign Row_2 = shift_register_1_q5 & bit_extender_1_out;  // AND_Gate and_4, 8 bits wide
  assign Row_3 = shift_register_1_q4 & bit_extender_1_out;  // AND_Gate and_5, 8 bits wide
  assign Row_4 = shift_register_1_q3 & bit_extender_1_out;  // AND_Gate and_6, 8 bits wide
  assign Row_5 = shift_register_1_q2 & bit_extender_1_out;  // AND_Gate and_7, 8 bits wide
  assign Row_6 = shift_register_1_q1 & bit_extender_1_out;  // AND_Gate and_8, 8 bits wide
  assign Row_7 = shift_register_1_q0 & bit_extender_1_out;  // AND_Gate and_9, 8 bits wide
endmodule

module TTL_7483 (
  input  B4,
  input  Cin,
  input  B1,
  input  A1,
  input  A4,
  input  A3,
  input  B3,
  input  B2,
  input  A2,
  output S4,
  output Cout,
  output S1,
  output S3,
  output S2
);

  wire adder_2_cout, adder_3_cout, adder_4_cout;

  Adder #(.width(1)) adder_1 (.a(A4), .b(B4), .out(S4), .cin(adder_2_cout), .cout(Cout));
  Adder #(.width(1)) adder_2 (.a(A3), .b(B3), .out(S3), .cin(adder_3_cout), .cout(adder_2_cout));
  Adder #(.width(1)) adder_3 (.a(A2), .b(B2), .out(S2), .cin(adder_4_cout), .cout(adder_3_cout));
  Adder #(.width(1)) adder_4 (.a(A1), .b(B1), .out(S1), .cin(Cin), .cout(adder_4_cout));
endmodule

module TTL_74173 (
  input  M,
  input  N,
  input  nG2,
  input  nG1,
  input  CLK,
  input  D1,
  input  D2,
  input  D3,
  input  D4,
  input  CLR,
  output Q1,
  output Q2,
  output Q3,
  output Q4
);

  wire and_1_out, and_2_out, and_3_out, and_4_out, and_5_out, and_6_out, and_7_out, and_8_out, and_9_out,
       and_10_out, d_ff_1_q, d_ff_1_qn, d_ff_2_q, d_ff_2_qn, d_ff_3_q, d_ff_3_qn, d_ff_4_q, d_ff_4_qn,
       not_1_out, not_2_out, not_3_out, not_4_out, not_5_out, not_6_out, not_7_out, not_8_out, not_9_out,
       not_10_out, not_11_out, not_12_out, not_13_out, not_14_out, not_15_out, or_1_out, or_2_out, or_3_out,
       or_4_out;

  not not_1 (not_1_out, CLK);
  not not_2 (not_2_out, CLR);
  and and_1 (and_1_out, ~M, ~N);  // AND_Gate
  and and_2 (and_2_out, ~nG2, ~nG1);  // AND_Gate
  not not_3 (not_3_out, and_2_out);
  and and_3 (and_3_out, d_ff_1_q, not_3_out);
  and and_4 (and_4_out, D1, and_2_out);
  and and_5 (and_5_out, d_ff_2_q, not_3_out);
  and and_6 (and_6_out, D2, and_2_out);
  and and_7 (and_7_out, d_ff_3_q, not_3_out);
  and and_8 (and_8_out, D3, and_2_out);
  and and_9 (and_9_out, d_ff_4_q, not_3_out);
  and and_10 (and_10_out, D4, and_2_out);
  D_Flip_Flop d_ff_1 (.D(or_1_out), .clk(not_4_out), .Q(d_ff_1_q), .Qn(d_ff_1_qn), .reset(not_5_out));  // open: preset
  or or_1 (or_1_out, and_3_out, and_4_out);
  not not_4 (not_4_out, not_1_out);
  not not_5 (not_5_out, not_2_out);
  D_Flip_Flop d_ff_2 (.D(or_2_out), .clk(not_6_out), .Q(d_ff_2_q), .Qn(d_ff_2_qn), .reset(not_7_out));  // open: preset
  or or_2 (or_2_out, and_5_out, and_6_out);
  not not_6 (not_6_out, not_1_out);
  not not_7 (not_7_out, not_2_out);
  D_Flip_Flop d_ff_3 (.D(or_3_out), .clk(not_8_out), .Q(d_ff_3_q), .Qn(d_ff_3_qn), .reset(not_9_out));  // open: preset
  or or_3 (or_3_out, and_7_out, and_8_out);
  not not_8 (not_8_out, not_1_out);
  not not_9 (not_9_out, not_2_out);
  D_Flip_Flop d_ff_4 (
    .D(or_4_out), .clk(not_10_out), .Q(d_ff_4_q), .Qn(d_ff_4_qn), .reset(not_11_out));  // open: preset
  or or_4 (or_4_out, and_9_out, and_10_out);
  not not_10 (not_10_out, not_1_out);
  not not_11 (not_11_out, not_2_out);
  not not_12 (not_12_out, d_ff_1_qn);
  assign Q1 = and_1_out ? not_12_out : 1'bz;  // Controlled_Buffer controlled_buffer_1
  not not_13 (not_13_out, d_ff_2_qn);
  assign Q2 = and_1_out ? not_13_out : 1'bz;  // Controlled_Buffer controlled_buffer_2
  not not_14 (not_14_out, d_ff_3_qn);
  assign Q3 = and_1_out ? not_14_out : 1'bz;  // Controlled_Buffer controlled_buffer_3
  not not_15 (not_15_out, d_ff_4_qn);
  assign Q4 = and_1_out ? not_15_out : 1'bz;  // Controlled_Buffer controlled_buffer_4
endmodule

module TTL_74175 (
  input  D1,
  input  D2,
  input  D3,
  input  D4,
  input  CLK,
  input  nCLR,
  output Q1,
  output nQ1,
  output Q2,
  output nQ2,
  output Q3,
  output nQ3,
  output Q4,
  output nQ4
);

  wire not_1_out, not_2_out, not_3_out, not_4_out, not_5_out, not_6_out, not_7_out, not_8_out, not_9_out,
       not_10_out, not_11_out;

  not not_1 (not_1_out, CLK);
  not not_2 (not_2_out, nCLR);
  not not_3 (not_3_out, not_2_out);
  D_Flip_Flop d_ff_1 (.D(D1), .clk(not_4_out), .Q(Q1), .Qn(nQ1), .reset(not_5_out));  // open: preset
  not not_4 (not_4_out, not_1_out);
  not not_5 (not_5_out, not_3_out);
  D_Flip_Flop d_ff_2 (.D(D2), .clk(not_6_out), .Q(Q2), .Qn(nQ2), .reset(not_7_out));  // open: preset
  not not_6 (not_6_out, not_1_out);
  not not_7 (not_7_out, not_3_out);
  D_Flip_Flop d_ff_3 (.D(D3), .clk(not_8_out), .Q(Q3), .Qn(nQ3), .reset(not_9_out));  // open: preset
  not not_8 (not_8_out, not_1_out);
  not not_9 (not_9_out, not_3_out);
  D_Flip_Flop d_ff_4 (.D(D4), .clk(not_10_out), .Q(Q4), .Qn(nQ4), .reset(not_11_out));  // open: preset
  not not_10 (not_10_out, not_1_out);
  not not_11 (not_11_out, not_3_out);
endmodule

module Accumulator_Module (
  input  [7:0] Data_in,
  input  [7:0] ALU_in,
  input  Sel_in,
  input  n_Write_en,
  input  Reset,
  input  CLK,
  output [7:0] Reg_out
);

  wire n74157_1_pin4, n74157_1_pin7, n74157_1_pin9, n74157_1_pin12, n74157_1_pin15, n74157_2_pin4,
       n74157_2_pin7, n74157_2_pin9, n74157_2_pin12;

  _74157 u_74157_1 (
    .pin1(Sel_in), .pin2(Data_in[7]), .pin3(ALU_in[7]), .pin4(n74157_1_pin4), .pin5(Data_in[6]),
    .pin6(ALU_in[6]), .pin7(n74157_1_pin7), .pin15(n74157_1_pin15), .pin14(Data_in[5]), .pin13(ALU_in[5]),
    .pin12(n74157_1_pin12), .pin11(Data_in[4]), .pin10(ALU_in[4]), .pin9(n74157_1_pin9));
  TTL_74173 ttl_74173_1 (
    .M(n74157_1_pin15), .N(n74157_1_pin15), .nG2(n74157_1_pin15), .nG1(n_Write_en), .CLK(CLK),
    .D1(n74157_1_pin4), .D2(n74157_1_pin7), .D3(n74157_1_pin12), .D4(n74157_1_pin9), .CLR(Reset),
    .Q1(Reg_out[7]), .Q2(Reg_out[6]), .Q3(Reg_out[5]), .Q4(Reg_out[4]));
  TTL_74173 ttl_74173_2 (
    .M(n74157_1_pin15), .N(n74157_1_pin15), .nG2(n74157_1_pin15), .nG1(n_Write_en), .CLK(CLK),
    .D1(n74157_2_pin4), .D2(n74157_2_pin7), .D3(n74157_2_pin12), .D4(n74157_2_pin9), .CLR(Reset),
    .Q1(Reg_out[3]), .Q2(Reg_out[2]), .Q3(Reg_out[1]), .Q4(Reg_out[0]));
  LED led_1 (.in(Reg_out[7]));
  LED led_2 (.in(Reg_out[6]));
  LED led_3 (.in(Reg_out[5]));
  LED led_4 (.in(Reg_out[4]));
  _74157 u_74157_2 (
    .pin1(Sel_in), .pin2(Data_in[3]), .pin3(ALU_in[3]), .pin4(n74157_2_pin4), .pin5(Data_in[2]),
    .pin6(ALU_in[2]), .pin7(n74157_2_pin7), .pin15(n74157_1_pin15), .pin14(Data_in[1]), .pin13(ALU_in[1]),
    .pin12(n74157_2_pin12), .pin11(Data_in[0]), .pin10(ALU_in[0]), .pin9(n74157_2_pin9));
  LED led_5 (.in(Reg_out[3]));
  LED led_6 (.in(Reg_out[2]));
  LED led_7 (.in(Reg_out[1]));
  LED led_8 (.in(Reg_out[0]));
  // also tied to GND on the sheet: n74157_1_pin15
endmodule

module ALU_Module (
  input  [7:0] Opcode,
  input  [7:0] A,
  input  [7:0] B,
  input  CF_in,
  output [7:0] Result,
  output ZF_out,
  output NF_out,
  output CF_out,
  output OF_out
);

  wire add0, add1, add2, add3, add4, add5, add6, add7, Adder_Cin, Adder_Cout, ALU_SHR_ROR, ALU_subtract,
       and0, and1, and2, and3, and4, and5, and6, and7, Bx0, Bx1, Bx2, Bx3, Bx4, Bx5, Bx6, Bx7, mux0, mux1,
       mux2, mux3, mux4, mux5, mux6, mux7, n7400_1_pin3, n7400_1_pin6, n7400_1_pin11, n7404_1_pin8,
       n7404_1_pin10, n7404_1_pin12, n7408_3_pin3, n7421_1_pin6, n7421_1_pin8, n7421_2_pin6, n7421_2_pin8,
       n7432_1_pin5, n7432_1_pin8, n7432_4_pin3, n7432_4_pin6, n7432_4_pin8, n7432_4_pin11, n7432_5_pin2,
       n7432_5_pin3, n7432_5_pin11, n7432_6_pin3, n7432_6_pin11, n74138_1_pin4, n74138_1_pin5, n74138_1_pin6,
       n74138_1_pin7, n74138_1_pin12, n74138_1_pin13, n74138_1_pin14, n74153_1_pin1, n74153_1_pin15,
       n74153_2_pin1, n74153_2_pin15, n74153_3_pin1, n74153_3_pin15, n74153_4_pin1, n74153_4_pin15,
       n74157_1_pin15, n74157_2_pin15, n74283_1_pin7, n_A_neg, n_B_neg, n_Op_sub, n_Out_neg, or0, or1, or2,
       or3, or4, or5, or6, or7, ROR_Cin, xor0, xor1, xor2, xor3, xor4, xor5, xor6, xor7;

  _74138 u_74138_1 (
    .pin1(Opcode[2]), .pin2(Opcode[3]), .pin3(Opcode[5]), .pin4(n74138_1_pin4), .pin5(n74138_1_pin5),
    .pin6(n74138_1_pin6), .pin7(n74138_1_pin7), .pin14(n74138_1_pin14), .pin13(n74138_1_pin13),
    .pin12(n74138_1_pin12));  // open: pin15, pin11, pin10, pin9
  _7486 u_7486_1 (
    .pin1(B[5]), .pin2(ALU_subtract), .pin3(Bx5), .pin4(B[4]), .pin5(ALU_subtract), .pin6(Bx4), .pin13(B[6]),
    .pin12(ALU_subtract), .pin11(Bx6), .pin10(B[7]), .pin9(ALU_subtract), .pin8(Bx7));
  _7408 u_7408_1 (
    .pin1(A[5]), .pin2(B[5]), .pin3(and5), .pin4(A[4]), .pin5(B[4]), .pin6(and4), .pin13(A[6]), .pin12(B[6]),
    .pin11(and6), .pin10(A[7]), .pin9(B[7]), .pin8(and7));
  _7486 u_7486_2 (
    .pin1(A[5]), .pin2(B[5]), .pin3(xor5), .pin4(A[4]), .pin5(B[4]), .pin6(xor4), .pin13(A[6]), .pin12(B[6]),
    .pin11(xor6), .pin10(A[7]), .pin9(B[7]), .pin8(xor7));
  _7404 u_7404_1 (
    .pin1(n74138_1_pin7), .pin2(ALU_SHR_ROR), .pin13(n74138_1_pin14), .pin12(n7404_1_pin12),
    .pin11(n74138_1_pin13), .pin10(n7404_1_pin10), .pin9(n74138_1_pin12), .pin8(n7404_1_pin8));  // open: pin3, pin4, pin5, pin6
  _7486 u_7486_3 (
    .pin1(B[1]), .pin2(ALU_subtract), .pin3(Bx1), .pin4(B[0]), .pin5(ALU_subtract), .pin6(Bx0), .pin13(B[2]),
    .pin12(ALU_subtract), .pin11(Bx2), .pin10(B[3]), .pin9(ALU_subtract), .pin8(Bx3));
  _7408 u_7408_2 (
    .pin1(A[1]), .pin2(B[1]), .pin3(and1), .pin4(A[0]), .pin5(B[0]), .pin6(and0), .pin13(A[2]), .pin12(B[2]),
    .pin11(and2), .pin10(A[3]), .pin9(B[3]), .pin8(and3));
  _7486 u_7486_4 (
    .pin1(A[1]), .pin2(B[1]), .pin3(xor1), .pin4(A[0]), .pin5(B[0]), .pin6(xor0), .pin13(A[2]), .pin12(B[2]),
    .pin11(xor2), .pin10(A[3]), .pin9(B[3]), .pin8(xor3));
  _7432 u_7432_1 (
    .pin4(n7404_1_pin12), .pin5(n7432_1_pin5), .pin6(Adder_Cin), .pin13(n7404_1_pin12), .pin12(n7404_1_pin8),
    .pin11(ALU_subtract), .pin10(n7404_1_pin10), .pin9(n7404_1_pin8), .pin8(n7432_1_pin8));  // open: pin1, pin2, pin3
  _74283 u_74283_1 (
    .pin1(add5), .pin2(Bx5), .pin3(A[5]), .pin4(add4), .pin5(A[4]), .pin6(Bx4), .pin7(n74283_1_pin7),
    .pin15(Bx6), .pin14(A[6]), .pin13(add6), .pin12(A[7]), .pin11(Bx7), .pin10(add7), .pin9(Adder_Cout));
  _7432 u_7432_2 (
    .pin1(A[5]), .pin2(B[5]), .pin3(or5), .pin4(A[4]), .pin5(B[4]), .pin6(or4), .pin13(A[6]), .pin12(B[6]),
    .pin11(or6), .pin10(A[7]), .pin9(B[7]), .pin8(or7));
  _7408 u_7408_3 (
    .pin1(ALU_SHR_ROR), .pin2(Opcode[4]), .pin3(n7408_3_pin3), .pin13(n7432_1_pin8), .pin12(CF_in),
    .pin11(n7432_1_pin5), .pin10(CF_in), .pin9(n7408_3_pin3), .pin8(ROR_Cin));  // open: pin4, pin5, pin6
  _74283 u_74283_2 (
    .pin1(add1), .pin2(Bx1), .pin3(A[1]), .pin4(add0), .pin5(A[0]), .pin6(Bx0), .pin7(Adder_Cin),
    .pin15(Bx2), .pin14(A[2]), .pin13(add2), .pin12(A[3]), .pin11(Bx3), .pin10(add3), .pin9(n74283_1_pin7));
  _7432 u_7432_3 (
    .pin1(A[1]), .pin2(B[1]), .pin3(or1), .pin4(A[0]), .pin5(B[0]), .pin6(or0), .pin13(A[2]), .pin12(B[2]),
    .pin11(or2), .pin10(A[3]), .pin9(B[3]), .pin8(or3));
  _74157 u_74157_1 (
    .pin1(Opcode[5]), .pin2(add5), .pin3(mux5), .pin4(Result[5]), .pin5(add4), .pin6(mux4), .pin7(Result[4]),
    .pin15(n74157_1_pin15), .pin14(add6), .pin13(mux6), .pin12(Result[6]), .pin11(add7), .pin10(mux7),
    .pin9(NF_out));
  _74153 u_74153_1 (
    .pin1(n74153_1_pin1), .pin2(Opcode[3]), .pin3(A[6]), .pin4(xor5), .pin5(or5), .pin6(and5), .pin7(mux5),
    .pin15(n74153_1_pin15), .pin14(Opcode[2]), .pin13(A[7]), .pin12(xor6), .pin11(or6), .pin10(and6),
    .pin9(mux6));
  _74153 u_74153_2 (
    .pin1(n74153_2_pin1), .pin2(Opcode[3]), .pin3(A[2]), .pin4(xor1), .pin5(or1), .pin6(and1), .pin7(mux1),
    .pin15(n74153_2_pin15), .pin14(Opcode[2]), .pin13(A[3]), .pin12(xor2), .pin11(or2), .pin10(and2),
    .pin9(mux2));
  _7432 u_7432_4 (
    .pin1(Result[5]), .pin2(Result[6]), .pin3(n7432_4_pin3), .pin4(n7432_4_pin3), .pin5(NF_out),
    .pin6(n7432_4_pin6), .pin13(Result[4]), .pin12(Result[3]), .pin11(n7432_4_pin11), .pin10(n7432_4_pin11),
    .pin9(Result[2]), .pin8(n7432_4_pin8));
  _7432 u_7432_5 (
    .pin1(n7432_4_pin6), .pin2(n7432_5_pin2), .pin3(n7432_5_pin3), .pin13(n7432_4_pin8), .pin12(Result[1]),
    .pin11(n7432_5_pin11), .pin10(n7432_5_pin11), .pin9(Result[0]), .pin8(n7432_5_pin2));  // open: pin4, pin5, pin6
  _7404 u_7404_2 (
    .pin1(Opcode[2]), .pin2(n_Op_sub), .pin3(NF_out), .pin4(n_Out_neg), .pin13(A[7]), .pin12(n_A_neg),
    .pin11(B[7]), .pin10(n_B_neg), .pin9(n7432_5_pin3), .pin8(ZF_out));  // open: pin5, pin6
  _74157 u_74157_2 (
    .pin1(Opcode[5]), .pin2(add1), .pin3(mux1), .pin4(Result[1]), .pin5(add0), .pin6(mux0), .pin7(Result[0]),
    .pin15(n74157_2_pin15), .pin14(add2), .pin13(mux2), .pin12(Result[2]), .pin11(add3), .pin10(mux3),
    .pin9(Result[3]));
  _74153 u_74153_3 (
    .pin1(n74153_3_pin1), .pin2(Opcode[3]), .pin3(A[5]), .pin4(xor4), .pin5(or4), .pin6(and4), .pin7(mux4),
    .pin15(n74153_3_pin15), .pin14(Opcode[2]), .pin13(ROR_Cin), .pin12(xor7), .pin11(or7), .pin10(and7),
    .pin9(mux7));
  _74153 u_74153_4 (
    .pin1(n74153_4_pin1), .pin2(Opcode[3]), .pin3(A[1]), .pin4(xor0), .pin5(or0), .pin6(and0), .pin7(mux0),
    .pin15(n74153_4_pin15), .pin14(Opcode[2]), .pin13(A[4]), .pin12(xor3), .pin11(or3), .pin10(and3),
    .pin9(mux3));
  _7421 u_7421_1 (
    .pin1(n_A_neg), .pin2(B[7]), .pin4(NF_out), .pin5(Opcode[2]), .pin6(n7421_1_pin6), .pin13(n_A_neg),
    .pin12(n_B_neg), .pin10(NF_out), .pin9(n_Op_sub), .pin8(n7421_1_pin8));  // open: pin3, pin11
  _7400 u_7400_1 (
    .pin1(Opcode[4]), .pin2(Opcode[4]), .pin3(n7400_1_pin3), .pin4(n7400_1_pin3), .pin5(Adder_Cout),
    .pin6(n7400_1_pin6), .pin13(ALU_SHR_ROR), .pin12(A[0]), .pin11(n7400_1_pin11), .pin10(n7400_1_pin11),
    .pin9(n7400_1_pin6), .pin8(CF_out));
  _7421 u_7421_2 (
    .pin1(A[7]), .pin2(n_B_neg), .pin4(n_Out_neg), .pin5(Opcode[2]), .pin6(n7421_2_pin6), .pin13(A[7]),
    .pin12(B[7]), .pin10(n_Out_neg), .pin9(n_Op_sub), .pin8(n7421_2_pin8));  // open: pin3, pin11
  _7432 u_7432_6 (
    .pin1(n7421_1_pin6), .pin2(n7421_2_pin6), .pin3(n7432_6_pin3), .pin13(n7421_1_pin8),
    .pin12(n7421_2_pin8), .pin11(n7432_6_pin11), .pin10(n7432_6_pin11), .pin9(n7432_6_pin3), .pin8(OF_out));  // open: pin4, pin5, pin6

  assign Result[7] = NF_out;
  // also tied to GND on the sheet: {n74138_1_pin4, n74138_1_pin5, n74153_1_pin1, n74153_2_pin1, n74157_1_pin15, n74153_1_pin15, n74153_2_pin15, n74153_3_pin1, n74153_4_pin1, n74157_2_pin15, n74153_3_pin15, n74153_4_pin15}
  // also tied to VCC on the sheet: n74138_1_pin6

  // Other names for the same wires on the sheet: ALU_A[7:0] = A; SHR_Cout = A[0]; shr0 = A[1]; shr1 = A[2];
  //   shr2 = A[3]; shr3 = A[4]; shr4 = A[5]; shr5 = A[6]; A_neg = A[7]; shr6 = A[7]; ALU_B[7:0] = B; B_neg = B[7];
  //   ALU_CF = CF_out; ALU_OF = OF_out; ALU_out[7:0] = {NF_out, Result[6:0]}; out0 = Result[0]; out1 = Result[1];
  //   out2 = Result[2]; out3 = Result[3]; out4 = Result[4]; out5 = Result[5]; out6 = Result[6]; ALU_NF = NF_out;
  //   out7 = NF_out; Out_neg = NF_out; ALU_ZF = ZF_out; Op_sub = Opcode[2]; S_CF = CF_in; shr7 = ROR_Cin
endmodule

module Register_Module (
  input  [7:0] Data_in,
  input  n_Write_en,
  input  Reset,
  input  CLK,
  output [7:0] Reg_out
);

  TTL_74173 ttl_74173_1 (
    .M(1'b0), .N(1'b0), .nG2(1'b0), .nG1(n_Write_en), .CLK(CLK), .D1(Data_in[7]), .D2(Data_in[6]),
    .D3(Data_in[5]), .D4(Data_in[4]), .CLR(Reset), .Q1(Reg_out[7]), .Q2(Reg_out[6]), .Q3(Reg_out[5]),
    .Q4(Reg_out[4]));
  TTL_74173 ttl_74173_2 (
    .M(1'b0), .N(1'b0), .nG2(1'b0), .nG1(n_Write_en), .CLK(CLK), .D1(Data_in[3]), .D2(Data_in[2]),
    .D3(Data_in[1]), .D4(Data_in[0]), .CLR(Reset), .Q1(Reg_out[3]), .Q2(Reg_out[2]), .Q3(Reg_out[1]),
    .Q4(Reg_out[0]));
  LED led_1 (.in(Reg_out[7]));
  LED led_2 (.in(Reg_out[6]));
  LED led_3 (.in(Reg_out[5]));
  LED led_4 (.in(Reg_out[4]));
  LED led_5 (.in(Reg_out[3]));
  LED led_6 (.in(Reg_out[2]));
  LED led_7 (.in(Reg_out[1]));
  LED led_8 (.in(Reg_out[0]));
endmodule

module Register_Tri_State_Module (
  input  [7:0] Reg_in,
  input  n_Data_en,
  input  n_Addr_en,
  output [7:0] Data,
  output [7:0] Addr
);

  wire n74541_1_pin19;

  _74541 u_74541_1 (
    .pin1(n_Data_en), .pin2(Reg_in[0]), .pin3(Reg_in[1]), .pin4(Reg_in[2]), .pin5(Reg_in[3]),
    .pin6(Reg_in[4]), .pin7(Reg_in[5]), .pin8(Reg_in[6]), .pin9(Reg_in[7]), .pin19(n74541_1_pin19),
    .pin18(Data[0]), .pin17(Data[1]), .pin16(Data[2]), .pin15(Data[3]), .pin14(Data[4]), .pin13(Data[5]),
    .pin12(Data[6]), .pin11(Data[7]));
  _74541 u_74541_2 (
    .pin1(n_Addr_en), .pin2(Reg_in[0]), .pin3(Reg_in[1]), .pin4(Reg_in[2]), .pin5(Reg_in[3]),
    .pin6(Reg_in[4]), .pin7(Reg_in[5]), .pin8(Reg_in[6]), .pin9(Reg_in[7]), .pin19(n74541_1_pin19),
    .pin18(Addr[0]), .pin17(Addr[1]), .pin16(Addr[2]), .pin15(Addr[3]), .pin14(Addr[4]), .pin13(Addr[5]),
    .pin12(Addr[6]), .pin11(Addr[7]));
  // also tied to GND on the sheet: n74541_1_pin19
endmodule

module PC_Module (
  input  Count_en,
  input  CLK,
  input  n_Reset,
  input  n_Jump_en,
  input  [7:0] Jump_addr,
  output [7:0] PC_out
);

  wire n74161_1_pin10, n74161_2_pin10, qn0, qn1, qn2, qn3, qn4, qn5, qn6, qn7;

  _74161 #(.ShowInternalStructure("true")) u_74161_1 (
    .pin1(n_Reset), .pin2(CLK), .pin3(qn4), .pin4(qn5), .pin5(qn6), .pin6(qn7), .pin7(Count_en),
    .pin14(PC_out[4]), .pin13(PC_out[5]), .pin12(PC_out[6]), .pin11(PC_out[7]), .pin10(n74161_1_pin10),
    .pin9(n_Jump_en));  // open: pin15
  _74157 #(.ShowInternalStructure("true")) u_74157_1 (
    .pin1(n_Jump_en), .pin2(Jump_addr[4]), .pin3(PC_out[4]), .pin4(qn4), .pin5(Jump_addr[5]),
    .pin6(PC_out[5]), .pin7(qn5), .pin14(Jump_addr[6]), .pin13(PC_out[6]), .pin12(qn6), .pin11(Jump_addr[7]),
    .pin10(PC_out[7]), .pin9(qn7));  // open: pin15
  _74161 #(.ShowInternalStructure("true")) u_74161_2 (
    .pin1(n_Reset), .pin2(CLK), .pin3(qn0), .pin4(qn1), .pin5(qn2), .pin6(qn3), .pin7(Count_en),
    .pin15(n74161_1_pin10), .pin14(PC_out[0]), .pin13(PC_out[1]), .pin12(PC_out[2]), .pin11(PC_out[3]),
    .pin10(n74161_2_pin10), .pin9(n_Jump_en));
  _74157 #(.ShowInternalStructure("true")) u_74157_2 (
    .pin1(n_Jump_en), .pin2(Jump_addr[0]), .pin3(PC_out[0]), .pin4(qn0), .pin5(Jump_addr[1]),
    .pin6(PC_out[1]), .pin7(qn1), .pin14(Jump_addr[2]), .pin13(PC_out[2]), .pin12(qn2), .pin11(Jump_addr[3]),
    .pin10(PC_out[3]), .pin9(qn3));  // open: pin15
  LED led_1 (.in(PC_out[7]));
  LED led_2 (.in(PC_out[6]));
  LED led_3 (.in(PC_out[5]));
  LED led_4 (.in(PC_out[4]));
  LED led_5 (.in(PC_out[3]));
  LED led_6 (.in(PC_out[0]));
  LED led_7 (.in(PC_out[2]));
  LED led_8 (.in(PC_out[1]));
  // also tied to VCC on the sheet: n74161_2_pin10

  // Other names for the same wires on the sheet: addr0 = Jump_addr[0]; addr1 = Jump_addr[1]; addr2 = Jump_addr[2];
  //   addr3 = Jump_addr[3]; addr4 = Jump_addr[4]; addr5 = Jump_addr[5]; addr6 = Jump_addr[6]; addr7 = Jump_addr[7];
  //   q0 = PC_out[0]; q1 = PC_out[1]; q2 = PC_out[2]; q3 = PC_out[3]; q4 = PC_out[4]; q5 = PC_out[5]; q6 = PC_out[6];
  //   q7 = PC_out[7]
endmodule

module Status_Flags_Module (
  input  ZF_in,
  input  NF_in,
  input  CF_in,
  input  OF_in,
  input  ALU_en,
  input  Set_CF,
  input  Set_OF,
  input  Reset,
  input  CLK,
  output ZF_out,
  output NF_out,
  output CF_out,
  output OF_out
);

  wire n7408_1_pin3, n7408_1_pin6, n7408_1_pin8, n7408_1_pin11, n7408_2_pin2, n7408_2_pin3, n7408_2_pin5,
       n7408_2_pin6, n7408_2_pin8, n7408_2_pin11, n7408_2_pin12, n7432_1_pin3, n7432_1_pin6, n7432_1_pin8,
       n7432_1_pin11;

  _7408 u_7408_1 (
    .pin1(CF_in), .pin2(Set_CF), .pin3(n7408_1_pin3), .pin4(OF_in), .pin5(Set_OF), .pin6(n7408_1_pin6),
    .pin13(ZF_in), .pin12(ALU_en), .pin11(n7408_1_pin11), .pin10(NF_in), .pin9(ALU_en), .pin8(n7408_1_pin8));
  _7408 u_7408_2 (
    .pin1(CF_out), .pin2(n7408_2_pin2), .pin3(n7408_2_pin3), .pin4(OF_out), .pin5(n7408_2_pin5),
    .pin6(n7408_2_pin6), .pin13(ZF_out), .pin12(n7408_2_pin12), .pin11(n7408_2_pin11), .pin10(NF_out),
    .pin9(n7408_2_pin12), .pin8(n7408_2_pin8));
  _7404 u_7404_1 (
    .pin13(ALU_en), .pin12(n7408_2_pin12), .pin11(Set_CF), .pin10(n7408_2_pin2), .pin9(Set_OF),
    .pin8(n7408_2_pin5));  // open: pin1, pin2, pin3, pin4, pin5, pin6
  _7432 u_7432_1 (
    .pin1(n7408_1_pin3), .pin2(n7408_2_pin3), .pin3(n7432_1_pin3), .pin4(n7408_1_pin6), .pin5(n7408_2_pin6),
    .pin6(n7432_1_pin6), .pin13(n7408_1_pin11), .pin12(n7408_2_pin11), .pin11(n7432_1_pin11),
    .pin10(n7408_1_pin8), .pin9(n7408_2_pin8), .pin8(n7432_1_pin8));
  TTL_74173 ttl_74173_1 (
    .M(1'b0), .N(1'b0), .nG2(1'b0), .nG1(1'b0), .CLK(CLK), .D1(n7432_1_pin11), .D2(n7432_1_pin8),
    .D3(n7432_1_pin3), .D4(n7432_1_pin6), .CLR(Reset), .Q1(ZF_out), .Q2(NF_out), .Q3(CF_out), .Q4(OF_out));
endmodule

module Mux_2_to_1_8_bit_Module (
  input  [7:0] A,
  input  [7:0] B,
  input  Sel,
  output [7:0] Y
);

  wire n74157_1_pin15;

  _74157 u_74157_1 (
    .pin1(Sel), .pin2(A[7]), .pin3(B[7]), .pin4(Y[7]), .pin5(A[6]), .pin6(B[6]), .pin7(Y[6]),
    .pin15(n74157_1_pin15), .pin14(A[5]), .pin13(B[5]), .pin12(Y[5]), .pin11(A[4]), .pin10(B[4]), .pin9(Y[4]));
  _74157 u_74157_2 (
    .pin1(Sel), .pin2(A[3]), .pin3(B[3]), .pin4(Y[3]), .pin5(A[2]), .pin6(B[2]), .pin7(Y[2]),
    .pin15(n74157_1_pin15), .pin14(A[1]), .pin13(B[1]), .pin12(Y[1]), .pin11(A[0]), .pin10(B[0]), .pin9(Y[0]));
  // also tied to GND on the sheet: n74157_1_pin15
endmodule

module Error_detector (
  input  in_1,
  output out_2
);

  wire pull_resistor_1_node, register_1_q;

  Pull_Resistor pull_resistor_1 (.node(pull_resistor_1_node));
  BitSelector #(.width(2)) bitselector_1 (.in(2'b11), .out(pull_resistor_1_node), .sel(out_2));
  Register #(.trigger("low"), .width(1)) register_1 (
    .D(in_1), .en(pull_resistor_1_node), .clk(1'b0), .Q(register_1_q));  // open: clr
  xnor xnor_1 (out_2, register_1_q, register_1_q);
endmodule
